// Logisim project DataPath.circ as structural Verilog
module main (
  input  in_1,
  input  in_2,
  input  in_3,
  input  [1:0] in_4,
  input  in_5,
  input  in_6,
  input  [1:0] in_7,
  input  in_8,
  input  in_9,
  input  in_10,
  input  [31:0] in_11,
  input  [31:0] in_12,
  input  [31:0] in_13,
  input  [31:0] in_14,
  output [5:0] out_15,
  output [5:0] out_16
);

  wire I, J, N, R, Z;
  wire [1:0] RF_D_SEL;
  wire [3:0] ALU_Op;
  wire [4:0] multiplexer_1_out, Rd, Rs, Rt;
  wire [15:0] instr_adress, k;
  wire [27:0] D;
  wire [31:0] A, ALU_Hi, ALU_OUT, ALU_Out_t, B, \const , Hi, Hi_Lo, instr, instruction, last_ALU, Lo,
       multiplexer_2_out, multiplexer_3_out, multiplexer_4_out, PC, Ram_Out;

  PC pc_1 (.in_2(in_2), .in_3(in_8), .in_4(in_5), .out_5(PC));  // open: in_1
  Instr__Fetcher instr_fetcher_1 (
    .in_1(in_11), .in_2(in_12), .in_3(in_13), .in_4(in_14), .in_5(PC), .INSTR__ADRESS(instr_adress),
    .instr(instr));
  Instruction_Decoder instruction_decoder_1 (
    .in_1(instruction), .Rs(Rs), .Rt(Rt), .out_11(k), .Dest(D), .J(J), .R(R), .I(I), .func_code(out_16),
    .out_3(out_15), .Rd(Rd));
  Register #(.width(32)) IR (.D(instr), .en(in_1), .Q(instruction), .clk(in_5), .clr(in_8));
  Multiplexer #(.width(5), .disabled(0), .enable("false")) multiplexer_1 (
    .in0(Rd), .in1(Rt), .out(multiplexer_1_out), .sel(I));
  Multiplexer #(.select(2), .width(32), .disabled(0), .enable("false")) multiplexer_2 (
    .in0(ALU_Out_t), .in1(A), .in2(Ram_Out), .in3(\const ), .out(multiplexer_2_out), .sel(RF_D_SEL));
  Multiplexer #(.select(2), .width(32), .disabled(0), .enable("false")) multiplexer_3 (
    .in0(B), .in1(32'h4), .in2(\const ), .in3({32{1'b0}}), .out(multiplexer_3_out), .sel(in_7));
  Multiplexer #(.select(2), .width(32), .disabled(0), .enable("false")) multiplexer_4 (
    .in0(A), .in1(PC), .in2(Hi_Lo), .out(multiplexer_4_out), .sel(in_4));  // open: in3
  Register_File register_file_1 (
    .in_1(multiplexer_2_out), .DA(multiplexer_1_out), .A(A), .B(B), .in_3(in_6), .in_7(in_5), .in_5(in_8),
    .SA(Rs), .SB(Rt));
  ALU_2 alu_1 (
    .Output(ALU_OUT), .Z_Flag(Z), .A(multiplexer_4_out), .B(multiplexer_3_out), .SEL(ALU_Op), .N_Flagt(N),
    .Hi_Lo(ALU_Hi));
  Register #(.width(32)) u_ALU_OUT (.D(ALU_OUT), .en(in_9), .Q(last_ALU), .clk(in_5), .clr(in_8));
  Register #(.width(32)) register_1 (.D(ALU_Hi), .en(in_10), .Q(Hi), .clk(in_5), .clr(in_8));
  Register #(.width(32)) register_2 (.D(ALU_OUT), .en(in_10), .Q(Lo), .clk(in_5), .clr(in_8));

  // Other names for the same wires on the sheet: Alu_Load = in_9; ALU_SEL_A[1:0] = in_4; ALU_SEL_B[1:0] = in_7;
  //   clk = in_5; DATA_RAM_2[31:0] = in_12; DATA_RAM_3[31:0] = in_13; DATA_RAM_4[31:0] = in_14;
  //   DATA_RAM__1[31:0] = in_11; Hi_Lo_Load = in_10; I_or_D = in_3; IR_Load = in_1; PC_en = in_2; RF_R_W = in_6;
  //   rst = in_8
endmodule

module Instr__Fetcher (
  input  [31:0] in_1,
  input  [31:0] in_2,
  input  [31:0] in_3,
  input  [31:0] in_4,
  input  [31:0] in_5,
  output [15:0] INSTR__ADRESS,
  output [31:0] instr
);

  Bit_Extender #(.in_width(30)) bit_extender_1 (.in(in_5[31:2]), .out(INSTR__ADRESS));
  Multiplexer #(.select(2), .width(32), .disabled(0), .enable("false")) multiplexer_1 (
    .in0(in_1), .in1(in_2), .in2(in_3), .in3(in_4), .out(instr), .sel(in_5[1:0]));

  // Other names for the same wires on the sheet: DATA_RAM_2[31:0] = in_2; DATA_RAM_3[31:0] = in_3;
  //   DATA_RAM_4[31:0] = in_4; DATA_RAM__1[31:0] = in_1; DATA_SEL[1:0] = in_5[1:0]; PC[31:0] = in_5;
  //   RAM_ADRESS[29:0] = in_5[31:2]

  // Notes on the sheet:
  //   Instruction Fetcher
endmodule

module Data_Fetcher (
  input  [31:0] in_1,
  input  [31:0] in_2,
  input  [31:0] in_3,
  input  [31:0] in_4,
  input  [31:0] in_5
);


  // Other names for the same wires on the sheet: DATA_RAM_2[31:0] = in_2; DATA_RAM_3[31:0] = in_3;
  //   DATA_RAM_4[31:0] = in_4; DATA_RAM__1[31:0] = in_1; RAM_INDEX[31:0] = in_5
endmodule

module Branch_Control (
  input  Negative_Flag,
  input  Zero_Flag,
  input  [31:0] IA,
  input  [31:0] k,
  input  [5:0] OP_Code,
  input  I_prime_m_I,
  output [31:0] IA_prime
);

  wire _0, _0_t, _0_t_t, A, and_3_out, and_6_out, AreZeros, B, C, D, E, Equal, JC, nand_1_out, nEqual,
       or_1_out, or_2_out;
  wire [31:0] multiplexer_1_out;

  Decoder #(.select(3), .enable("false")) decoder_1 (
    .out1(_0_t), .out4(Equal), .out5(nEqual), .out6(_0), .out7(_0_t_t), .sel(OP_Code[2:0]));  // open: out0, out2, out3
  Comparator #(.width(3)) comparator_1 (.a(3'b000), .b(OP_Code[5:3]), .eq(AreZeros));  // open: gt, lt
  Multiplexer #(.select(2), .width(32), .enable("false")) multiplexer_1 (
    .in0(32'h4), .in1(k), .out(multiplexer_1_out));  // open: in2, in3, sel
  and and_1 (A, nEqual, ~Zero_Flag);  // AND_Gate
  and and_2 (B, Zero_Flag, Equal);
  or or_1 (or_1_out, Zero_Flag, Negative_Flag);
  Adder #(.width(32)) adder_1 (.a(IA), .b(multiplexer_1_out), .out(IA_prime));  // open: cin, cout
  or or_2 (or_2_out, A, B, C, D, E);
  and and_3 (and_3_out, AreZeros, I_prime_m_I);
  and and_4 (C, _0, or_1_out);
  and and_5 (JC, or_2_out, and_3_out);
  nand nand_1 (nand_1_out, Negative_Flag, Zero_Flag);
  and and_6 (and_6_out, Negative_Flag, ~Zero_Flag);  // AND_Gate
  and and_7 (D, _0_t_t, nand_1_out);
  and and_8 (E, _0_t, and_6_out);

  // Other names for the same wires on the sheet: I = I_prime_m_I; Nega = Negative_Flag; Last[2:0] = OP_Code[2:0];
  //   Firsts[2:0] = OP_Code[5:3]; Zero = Zero_Flag

  // Notes on the sheet:
  //   BRANCH CONTROL
endmodule

module Instruction_Decoder (
  input  [31:0] in_1,
  output I,
  output [5:0] out_3,
  output J,
  output R,
  output [5:0] func_code,
  output [4:0] Rd,
  output [4:0] Rt,
  output [4:0] Rs,
  output [27:0] Dest,
  output [15:0] out_11
);

  Type_Decoder type_decoder_1 (.in_1(in_1[31:26]), .I(I), .J(J), .R(R));

  assign Dest = {in_1[25:0], 2'b00};
  assign func_code = in_1[5:0];
  assign out_3 = in_1[31:26];
  assign out_11 = in_1[15:0];
  assign Rd = in_1[15:11];
  assign Rs = in_1[25:21];
  assign Rt = in_1[20:16];

  // Other names for the same wires on the sheet: D[25:0] = in_1[25:0]; instruct[31:0] = in_1; k[15:0] = in_1[15:0];
  //   op_code[5:0] = in_1[31:26]

  // Notes on the sheet:
  //   INSTRUCTION DECODER
endmodule

module Type_Decoder (
  input  [5:0] in_1,
  output I,
  output J,
  output R
);

  wire and_1_out, and_3_out, and_4_out, D___E___F___V___nD___nE___nF, nA___nB___nC, nD___nE___nF;

  nor nor_1 (nD___nE___nF, in_1[2], in_1[1], in_1[0]);
  and and_1 (and_1_out, in_1[2], in_1[1], in_1[0]);
  and and_2 (J, nA___nB___nC, ~in_1[2], in_1[1], ~in_1[0]);  // AND_Gate
  or or_1 (D___E___F___V___nD___nE___nF, nD___nE___nF, and_1_out);
  nor nor_2 (nA___nB___nC, in_1[5], in_1[4], in_1[3]);
  and and_3 (and_3_out, nA___nB___nC, nD___nE___nF);
  and and_4 (and_4_out, in_1[5], in_1[4], in_1[3], D___E___F___V___nD___nE___nF);
  or or_2 (R, and_3_out, and_4_out);
  nor nor_3 (I, J, R);

  // Other names for the same wires on the sheet: F = in_1[0]; E = in_1[1]; D = in_1[2]; C = in_1[3]; B = in_1[4];
  //   A = in_1[5]

  // Notes on the sheet:
  //   TYPE DECODER
endmodule

module ALU_2 (
  input  [31:0] A,
  input  [31:0] B,
  input  [3:0] SEL,
  output [31:0] Output,
  output Z_Flag,
  output N_Flagt,
  output [31:0] Hi_Lo
);

  wire comparator_1_lt, comparator_2_lt;
  wire [31:0] adder_1_out, and_1_out, bit_extender_1_out, bit_extender_2_out, divider_1_out,
       divisor_con_signo_1_div, Hi, Hi_Sign, multiplicador_con_signo_1_lo, multiplier_1_out, nor_1_out,
       not_1_out, or_1_out, Rest, Rest_Sign, subtractor_1_out, xor_1_out;

  Multiplier #(.width(32)) multiplier_1 (.a(B), .b(A), .out(multiplier_1_out), .cout(Hi));  // open: cin
  Divider #(.width(32)) divider_1 (.a(A), .b(B), .out(divider_1_out), .rem(Rest));  // open: upper
  Multiplicador_Con_Signo multiplicador_con_signo_1 (.A(A), .B(B), .Lo(multiplicador_con_signo_1_lo), .Hi(Hi_Sign));
  Divisor_con_Signo divisor_con_signo_1 (.A(A), .B(B), .Div(divisor_con_signo_1_div), .Rest(Rest_Sign));
  assign and_1_out = A & B;  // AND_Gate and_1, 32 bits wide
  assign or_1_out = A | B;  // OR_Gate or_1, 32 bits wide
  assign nor_1_out = ~(A | B);  // NOR_Gate nor_1, 32 bits wide
  assign xor_1_out = A ^ B;  // XOR_Gate xor_1, 32 bits wide
  assign not_1_out = ~A;  // NOT_Gate not_1, 32 bits wide
  Comparator #(.width(32), .mode("unsigned")) comparator_1 (.a(A), .b(B), .lt(comparator_1_lt));  // open: gt, eq
  Comparator #(.width(32)) comparator_2 (.a(B), .b(A), .lt(comparator_2_lt));  // open: gt, eq
  Adder #(.width(32)) adder_1 (.a(B), .b(A), .out(adder_1_out));  // open: cin, cout
  Subtractor #(.width(32)) subtractor_1 (.a(B), .b(A), .out(subtractor_1_out));  // open: bin, bout
  assign bit_extender_1_out = {{31{1'b0}}, comparator_1_lt};  // Bit_Extender bit_extender_1
  assign bit_extender_2_out = {{31{1'b0}}, comparator_2_lt};  // Bit_Extender bit_extender_2
  Multiplexer #(.select(4), .width(32), .enable("false")) multiplexer_1 (
    .in0(multiplier_1_out), .in1(divider_1_out), .in2(multiplicador_con_signo_1_lo),
    .in3(divisor_con_signo_1_div), .in4(and_1_out), .in5(or_1_out), .in6(nor_1_out), .in7(xor_1_out),
    .in8(not_1_out), .in9(bit_extender_1_out), .in10(bit_extender_2_out), .in11(adder_1_out),
    .in12(subtractor_1_out), .out(Output), .sel(SEL));  // open: in13, in14, in15
  Multiplexer #(.select(2), .width(32), .enable("false")) multiplexer_2 (
    .in0(Hi), .in1(Rest), .in2(Hi_Sign), .in3(Rest_Sign), .out(Hi_Lo), .sel(SEL[1:0]));
  Comparator #(.width(32)) comparator_3 (.a(Output), .b({32{1'b0}}), .eq(Z_Flag), .lt(N_Flagt));  // open: gt

  // Other names for the same wires on the sheet: Selector[3:0] = SEL

  // Notes on the sheet:
  //   ARITHMETIC LOGIC UNIT(ALU)
endmodule

module Multiplicador_Con_Signo (
  input  [31:0] A,
  input  [31:0] B,
  output [31:0] Lo,
  output [31:0] Hi
);

  wire [30:0] Com_a2_A, Com_a2_B, multiplexer_1_out, multiplexer_2_out;

  Negator #(.width(31)) negator_1 (.in(A[30:0]), .out(Com_a2_A));
  Negator #(.width(31)) negator_2 (.in(B[30:0]), .out(Com_a2_B));
  xor xor_1 (Hi[31], B[31], A[31]);
  Multiplexer #(.width(31), .enable("false")) multiplexer_1 (
    .in0(A[30:0]), .in1(Com_a2_A), .out(multiplexer_1_out), .sel(A[31]));
  Multiplexer #(.width(31), .enable("false")) multiplexer_2 (
    .in0(B[30:0]), .in1(Com_a2_B), .out(multiplexer_2_out), .sel(B[31]));
  Multiplier #(.width(31)) multiplier_1 (
    .a(multiplexer_1_out), .b(multiplexer_2_out), .out(Lo[30:0]), .cout({Hi[29:0], Lo[31]}));  // open: cin

  assign Hi[30] = 1'b0;

  // Other names for the same wires on the sheet: A_t[30:0] = A[30:0]; Sign_A = A[31]; B_t[30:0] = B[30:0];
  //   Sign_B = B[31]; Hi_Mult[30:0] = {Hi[29:0], Lo[31]}; Sign = Hi[31]; Mult[30:0] = Lo[30:0]

  // Notes on the sheet:
  //   Multiplicador Con Signo
endmodule

module Divisor_con_Signo (
  input  [31:0] A,
  input  [31:0] B,
  output [31:0] Div,
  output [31:0] Rest
);

  wire [30:0] Com_a2_A, Com_a2_B, Current, multiplexer_1_out, multiplexer_2_out, negator_3_out;

  Negator #(.width(31)) negator_1 (.in(A[30:0]), .out(Com_a2_A));
  Negator #(.width(31)) negator_2 (.in(B[30:0]), .out(Com_a2_B));
  xor xor_1 (Div[31], B[31], A[31]);
  Multiplexer #(.width(31), .enable("false")) multiplexer_1 (
    .in0(A[30:0]), .in1(Com_a2_A), .out(multiplexer_1_out), .sel(A[31]));
  Multiplexer #(.width(31), .enable("false")) multiplexer_2 (
    .in0(B[30:0]), .in1(Com_a2_B), .out(multiplexer_2_out), .sel(B[31]));
  Negator #(.width(31)) negator_3 (.in(Current), .out(negator_3_out));
  Multiplexer #(.width(31), .enable("false")) multiplexer_3 (
    .in0(Current), .in1(negator_3_out), .out(Div[30:0]), .sel(Div[31]));
  Divider #(.width(31)) divider_1 (
    .a(multiplexer_1_out), .b(multiplexer_2_out), .out(Current), .rem(Rest[30:0]));  // open: upper

  assign Rest[31] = 1'b0;

  // Other names for the same wires on the sheet: A_t[30:0] = A[30:0]; Sign_A = A[31]; B_t[30:0] = B[30:0];
  //   Sign_B = B[31]; Div_t[30:0] = Div[30:0]; Sign = Div[31]; Rest_t[30:0] = Rest[30:0]

  // Notes on the sheet:
  //   Divisor Con Signo
endmodule

module Register_File (
  input  [31:0] in_1,
  input  [4:0] DA,
  input  in_3,
  input  [4:0] SA,
  input  in_5,
  input  [4:0] SB,
  input  in_7,
  output [31:0] A,
  output [31:0] B
);

  wire a0, a1, a2, a3, a4, a5, a6, a7, a8, a9, a10, a11, a12, a13, a14, a15, a16, a17, a18, a19, a20, a21,
       a22, a23, a24, a25, a26, a27, a28, a29, a30, a31;
  wire [31:0] q0, q1, q2, q3, q4, q5, q6, q7, q8, q9, q10, q11, q12, q13, q14, q15, q16, q17, q18, q19, q20,
       q21, q22, q23, q24, q25, q26, q27, q28, q29, q30, q31;

  Decoder #(.select(5), .disabled(0)) decoder_1 (
    .out0(a0), .out1(a1), .out2(a2), .out3(a3), .out4(a4), .out5(a5), .out6(a6), .out7(a7), .out8(a8),
    .out9(a9), .out10(a10), .out11(a11), .out12(a12), .out13(a13), .out14(a14), .out15(a15), .out16(a31),
    .out17(a30), .out18(a29), .out19(a28), .out20(a27), .out21(a26), .out22(a25), .out23(a24), .out24(a23),
    .out25(a22), .out26(a21), .out27(a20), .out28(a19), .out29(a18), .out30(a17), .out31(a16), .sel(DA),
    .en(in_3));
  Register #(.width(32)) R0 (.D({32{1'b0}}), .en(a0), .Q(q0), .clk(in_7), .clr(in_5));
  Register #(.width(32)) R4 (.D(in_1), .en(a4), .Q(q4), .clk(in_7), .clr(in_5));
  Register #(.width(32)) R8 (.D(in_1), .en(a8), .Q(q8), .clk(in_7), .clr(in_5));
  Register #(.width(32)) R12 (.D(in_1), .en(a12), .Q(q12), .clk(in_7), .clr(in_5));
  Register #(.width(32)) R16 (.D(in_1), .en(a16), .Q(q16), .clk(in_7), .clr(in_5));
  Register #(.width(32)) R20 (.D(in_1), .en(a20), .Q(q20), .clk(in_7), .clr(in_5));
  Register #(.width(32)) R24 (.D(in_1), .en(a24), .Q(q24), .clk(in_7), .clr(in_5));
  Register #(.width(32)) R28 (.D(in_1), .en(a28), .Q(q28), .clk(in_7), .clr(in_5));
  Register #(.width(32)) R1 (.D(in_1), .en(a1), .Q(q1), .clk(in_7), .clr(in_5));
  Register #(.width(32)) R5 (.D(in_1), .en(a5), .Q(q5), .clk(in_7), .clr(in_5));
  Register #(.width(32)) R9 (.D(in_1), .en(a9), .Q(q9), .clk(in_7), .clr(in_5));
  Register #(.width(32)) R13 (.D(in_1), .en(a13), .Q(q13), .clk(in_7), .clr(in_5));
  Register #(.width(32)) R17 (.D(in_1), .en(a17), .Q(q17), .clk(in_7), .clr(in_5));
  Register #(.width(32)) R21 (.D(in_1), .en(a21), .Q(q21), .clk(in_7), .clr(in_5));
  Register #(.width(32)) R25 (.D(in_1), .en(a25), .Q(q25), .clk(in_7), .clr(in_5));
  Register #(.width(32)) R29 (.D(in_1), .en(a29), .Q(q29), .clk(in_7), .clr(in_5));
  Register #(.width(32)) R2 (.D(in_1), .en(a2), .Q(q2), .clk(in_7), .clr(in_5));
  Register #(.width(32)) R6 (.D(in_1), .en(a6), .Q(q6), .clk(in_7), .clr(in_5));
  Register #(.width(32)) R10 (.D(in_1), .en(a10), .Q(q10), .clk(in_7), .clr(in_5));
  Register #(.width(32)) R14 (.D(in_1), .en(a14), .Q(q14), .clk(in_7), .clr(in_5));
  Register #(.width(32)) R18 (.D(in_1), .en(a18), .Q(q18), .clk(in_7), .clr(in_5));
  Register #(.width(32)) R22 (.D(in_1), .en(a22), .Q(q22), .clk(in_7), .clr(in_5));
  Register #(.width(32)) R26 (.D(in_1), .en(a26), .Q(q26), .clk(in_7), .clr(in_5));
  Register #(.width(32)) R30 (.D(in_1), .en(a30), .Q(q30), .clk(in_7), .clr(in_5));
  Register #(.width(32)) R3 (.D(in_1), .en(a3), .Q(q3), .clk(in_7), .clr(in_5));
  Register #(.width(32)) R7 (.D(in_1), .en(a7), .Q(q7), .clk(in_7), .clr(in_5));
  Register #(.width(32)) R11 (.D(in_1), .en(a11), .Q(q11), .clk(in_7), .clr(in_5));
  Register #(.width(32)) R15 (.D(in_1), .en(a15), .Q(q15), .clk(in_7), .clr(in_5));
  Register #(.width(32)) R19 (.D(in_1), .en(a19), .Q(q19), .clk(in_7), .clr(in_5));
  Register #(.width(32)) R23 (.D(in_1), .en(a23), .Q(q23), .clk(in_7), .clr(in_5));
  Register #(.width(32)) R27 (.D(in_1), .en(a27), .Q(q27), .clk(in_7), .clr(in_5));
  Register #(.width(32)) R31 (.D(in_1), .en(a31), .Q(q31), .clk(in_7), .clr(in_5));
  Multiplexer #(.select(5), .width(32), .enable("false")) multiplexer_1 (
    .in0(q0), .in1(q1), .in2(q2), .in3(q3), .in4(q4), .in5(q5), .in6(q6), .in7(q7), .in8(q8), .in9(q9),
    .in10(q10), .in11(q11), .in12(q12), .in13(q13), .in14(q14), .in15(q15), .in16(q16), .in17(q17),
    .in18(q18), .in19(q19), .in20(q20), .in21(q21), .in22(q22), .in23(q23), .in24(q24), .in25(q25),
    .in26(q26), .in27(q27), .in28(q28), .in29(q29), .in30(q30), .in31(q31), .out(A), .sel(SA));
  Multiplexer #(.select(5), .width(32), .enable("false")) multiplexer_2 (
    .in0(q0), .in1(q1), .in2(q2), .in3(q3), .in4(q4), .in5(q5), .in6(q6), .in7(q7), .in8(q8), .in9(q9),
    .in10(q10), .in11(q11), .in12(q12), .in13(q13), .in14(q14), .in15(q15), .in16(q16), .in17(q17),
    .in18(q18), .in19(q19), .in20(q20), .in21(q21), .in22(q22), .in23(q23), .in24(q24), .in25(q25),
    .in26(q26), .in27(q27), .in28(q28), .in29(q29), .in30(q30), .in31(q31), .out(B), .sel(SB));

  // Other names for the same wires on the sheet: clk = in_7; DI[31:0] = in_1; R_W = in_3; rst = in_5

  // Notes on the sheet:
  //   REGISTER FILE
  //   Control Signals
  //   Input Register
  //   Registers
  //   Output Registers
endmodule

module PC (
  input  [31:0] in_1,
  input  in_2,
  input  in_3,
  input  in_4,
  output [31:0] out_5
);

  Register #(.width(32)) PC (.D(in_1), .en(in_2), .Q(out_5), .clk(in_4), .clr(in_3));

  // Other names for the same wires on the sheet: clk = in_4; en = in_2; PC[31:0] = out_5; PC_prime[31:0] = in_1;
  //   rst = in_3
endmodule
