// Logisim project RF.circ as structural Verilog: 2 circuits, main circuit main
module main (
  input  [31:0] DI,
  input  [4:0] DA,
  input  [4:0] SA,
  input  rst,
  input  R_W,
  input  CLOCK,
  input  [4:0] SB,
  output [31:0] A,
  output [31:0] B
);

  wire a0, a1, a2, a3, a4, a5, a6, a7, a8, a9, a10, a11, a12, a13, a14, a15, a16, a17, a18, a19, a20, a21,
       a22, a23, a24, a25, a26, a27, a28, a29, a30, a31, and_1_out;
  wire [31:0] q0, q1, q2, q3, q4, q5, q6, q7, q8, q9, q10, q11, q12, q13, q14, q15, q16, q17, q18, q19, q20,
       q21, q22, q23, q24, q25, q26, q27, q28, q29, q30, q31;

  Decoder #(.select(5)) decoder_1 (
    .out0(a0), .out1(a1), .out2(a2), .out3(a3), .out4(a4), .out5(a5), .out6(a6), .out7(a7), .out8(a8),
    .out9(a9), .out10(a10), .out11(a11), .out12(a12), .out13(a13), .out14(a14), .out15(a15), .out16(a31),
    .out17(a30), .out18(a29), .out19(a28), .out20(a27), .out21(a26), .out22(a25), .out23(a24), .out24(a23),
    .out25(a22), .out26(a21), .out27(a20), .out28(a19), .out29(a18), .out30(a17), .out31(a16), .sel(DA));  // open: en
  and and_1 (and_1_out, R_W, CLOCK);
  Register #(.width(32)) R0 (.D(DI), .en(a0), .Q(q0), .clk(and_1_out), .clr(rst));
  Register #(.width(32)) R4 (.D(DI), .en(a4), .Q(q4), .clk(and_1_out), .clr(rst));
  Register #(.width(32)) R8 (.D(DI), .en(a8), .Q(q8), .clk(and_1_out), .clr(rst));
  Register #(.width(32)) R12 (.D(DI), .en(a12), .Q(q12), .clk(and_1_out), .clr(rst));
  Register #(.width(32)) R16 (.D(DI), .en(a16), .Q(q16), .clk(and_1_out), .clr(rst));
  Register #(.width(32)) R20 (.D(DI), .en(a20), .Q(q20), .clk(and_1_out), .clr(rst));
  Register #(.width(32)) R24 (.D(DI), .en(a24), .Q(q24), .clk(and_1_out), .clr(rst));
  Register #(.width(32)) R28 (.D(DI), .en(a28), .Q(q28), .clk(and_1_out), .clr(rst));
  Register #(.width(32)) R1 (.D(DI), .en(a1), .Q(q1), .clk(and_1_out), .clr(rst));
  Register #(.width(32)) R5 (.D(DI), .en(a5), .Q(q5), .clk(and_1_out), .clr(rst));
  Register #(.width(32)) R9 (.D(DI), .en(a9), .Q(q9), .clk(and_1_out), .clr(rst));
  Register #(.width(32)) R13 (.D(DI), .en(a13), .Q(q13), .clk(and_1_out), .clr(rst));
  Register #(.width(32)) R17 (.D(DI), .en(a17), .Q(q17), .clk(and_1_out), .clr(rst));
  Register #(.width(32)) R21 (.D(DI), .en(a21), .Q(q21), .clk(and_1_out), .clr(rst));
  Register #(.width(32)) R25 (.D(DI), .en(a25), .Q(q25), .clk(and_1_out), .clr(rst));
  Register #(.width(32)) R29 (.D(DI), .en(a29), .Q(q29), .clk(and_1_out), .clr(rst));
  Register #(.width(32)) R2 (.D(DI), .en(a2), .Q(q2), .clk(and_1_out), .clr(rst));
  Register #(.width(32)) R6 (.D(DI), .en(a6), .Q(q6), .clk(and_1_out), .clr(rst));
  Register #(.width(32)) R10 (.D(DI), .en(a10), .Q(q10), .clk(and_1_out), .clr(rst));
  Register #(.width(32)) R14 (.D(DI), .en(a14), .Q(q14), .clk(and_1_out), .clr(rst));
  Register #(.width(32)) R18 (.D(DI), .en(a18), .Q(q18), .clk(and_1_out), .clr(rst));
  Register #(.width(32)) R22 (.D(DI), .en(a22), .Q(q22), .clk(and_1_out), .clr(rst));
  Register #(.width(32)) R26 (.D(DI), .en(a26), .Q(q26), .clk(and_1_out), .clr(rst));
  Register #(.width(32)) R30 (.D(DI), .en(a30), .Q(q30), .clk(and_1_out), .clr(rst));
  Register #(.width(32)) R3 (.D(DI), .en(a3), .Q(q3), .clk(and_1_out), .clr(rst));
  Register #(.width(32)) R7 (.D(DI), .en(a7), .Q(q7), .clk(and_1_out), .clr(rst));
  Register #(.width(32)) R11 (.D(DI), .en(a11), .Q(q11), .clk(and_1_out), .clr(rst));
  Register #(.width(32)) R15 (.D(DI), .en(a15), .Q(q15), .clk(and_1_out), .clr(rst));
  Register #(.width(32)) R19 (.D(DI), .en(a19), .Q(q19), .clk(and_1_out), .clr(rst));
  Register #(.width(32)) R23 (.D(DI), .en(a23), .Q(q23), .clk(and_1_out), .clr(rst));
  Register #(.width(32)) R27 (.D(DI), .en(a27), .Q(q27), .clk(and_1_out), .clr(rst));
  Register #(.width(32)) R31 (.D(DI), .en(a31), .Q(q31), .clk(and_1_out), .clr(rst));
  Multiplexer #(.select(5), .width(32)) multiplexer_1 (
    .in0(q0), .in1(q1), .in2(q2), .in3(q3), .in4(q4), .in5(q5), .in6(q6), .in7(q7), .in8(q8), .in9(q9),
    .in10(q10), .in11(q11), .in12(q12), .in13(q13), .in14(q14), .in15(q15), .in16(q16), .in17(q17),
    .in18(q18), .in19(q19), .in20(q20), .in21(q21), .in22(q22), .in23(q23), .in24(q24), .in25(q25),
    .in26(q26), .in27(q27), .in28(q28), .in29(q29), .in30(q30), .in31(q31), .out(A), .sel(SA));  // open: en
  Multiplexer #(.select(5), .width(32)) multiplexer_2 (
    .in0(q0), .in1(q1), .in2(q2), .in3(q3), .in4(q4), .in5(q5), .in6(q6), .in7(q7), .in8(q8), .in9(q9),
    .in10(q10), .in11(q11), .in12(q12), .in13(q13), .in14(q14), .in15(q15), .in16(q16), .in17(q17),
    .in18(q18), .in19(q19), .in20(q20), .in21(q21), .in22(q22), .in23(q23), .in24(q24), .in25(q25),
    .in26(q26), .in27(q27), .in28(q28), .in29(q29), .in30(q30), .in31(q31), .out(B), .sel(SB));  // open: en

  // Notes on the sheet:
  //   REGISTER FILE
endmodule

module PRUEBA (
  input  [31:0] in_1,
  input  in_2,
  input  in_3,
  input  [4:0] in_4,
  input  [4:0] in_5,
  input  [4:0] in_6,
  output [31:0] out_7,
  output [31:0] out_8
);

  wire clock_1_out;

  Clock clock_1 (.out(clock_1_out));
  main main_1 (
    .DI(in_1), .DA(in_5), .A(out_7), .B(out_8), .R_W(in_2), .CLOCK(clock_1_out), .rst(in_3), .SA(in_4),
    .SB(in_6));
endmodule
