// Logisim project s-mips.circ as structural Verilog
module S_MIPS_Board (
  input  DESHABILITAR_DISPATCHER,
  output halt
);

  wire button_1_out, CLK, CS, d_ff_1_q, LCLR, LoadRAM, LoadRAMOn, LW, R_R_W, R_W, ram_dispatcher_1_finished,
       RCS, Reset_out, RST, TTY_EN;
  wire [2:0] KDB;
  wire [3:0] LMask, Mask, ram_1_read_time, ram_1_write_time, RMask;
  wire [6:0] KDB_DATA, TTY_DATA;
  wire [15:0] Addr, LAddr, RAddr;
  wire [31:0] I0, I1, I2, I3, LData, ram_1_data_out_0, ram_1_data_out_1, ram_1_data_out_2, ram_1_data_out_3,
       RI0, RI1, RI2, RI3;

  TTY #(.rows(25), .cols(80)) tty_1 (.data(TTY_DATA), .clk(CLK), .we(TTY_EN), .clr(RST));
  not not_1 (LoadRAMOn, ram_dispatcher_1_finished);
  RAM_Dispatcher ram_dispatcher_1 (
    .WriteTime(ram_1_write_time), .Clock(CLK), .Data(LData), .Address(LAddr), .Mask(LMask),
    .Finished(ram_dispatcher_1_finished), .Write(LW), .CLR(LCLR));
  Keyboard #(.buflen(64)) keyboard_1 (.clk(CLK), .re(KDB[0]), .avail(KDB[2]), .data(KDB_DATA));  // open: clr
  RAM ram_1 (
    .Address(RAddr), .Data_Out_0(ram_1_data_out_0), .Data_Out_1(ram_1_data_out_1),
    .Data_Out_2(ram_1_data_out_2), .Data_Out_3(ram_1_data_out_3), .Data_In_0(RI0), .Data_In_1(RI1),
    .Data_In_2(RI2), .Data_In_3(RI3), .Mask(RMask), .nRead_Write(R_R_W), .Chip_Select(RCS),
    .Read_Time(ram_1_read_time), .Reset(button_1_out), .Write_Time(ram_1_write_time));
  Button button_1 (.out(button_1_out));
  D_Flip_Flop d_ff_1 (.clk(CLK), .D(1'b1), .Q(d_ff_1_q), .reset(Reset_out));  // open: Qn, preset, en
  Button Reset (.out(Reset_out));
  S_MIPS s_mips_1 (
    .Kbd_Enable(KDB[0]), .Address(Addr), .Kbd_Clear(KDB[1]), .Kbd_Available(KDB[2]), .RAM_In_0(I0),
    .Kbd_ASCII_Data(KDB_DATA), .RAM_In_1(I1), .TTY_Enable(TTY_EN), .RAM_In_2(I2), .RAM_In_3(I3),
    .TTY_ASCII_Data(TTY_DATA), .Reset(RST), .RAM_Out_0(ram_1_data_out_0), .Clock(CLK),
    .RAM_Out_1(ram_1_data_out_1), .Stop(halt), .RAM_Out_2(ram_1_data_out_2), .RAM_Out_3(ram_1_data_out_3),
    .Mask(Mask), .Read_Time(ram_1_read_time), .Write_Time(ram_1_write_time), .nRead_Write(R_W),
    .Chip_Select(CS));
  D_Flip_Flop d_ff_2 (.clk(CLK), .D(d_ff_1_q), .Qn(LCLR), .reset(Reset_out));  // open: Q, preset, en
  or or_1 (RST, LCLR, LoadRAM);
  Clock clock_1 (.out(CLK));
  Multiplexer #(.width(32), .enable("false")) multiplexer_1 (.in0(I0), .in1(LData), .out(RI0), .sel(LoadRAM));
  Multiplexer #(.width(32), .enable("false")) multiplexer_2 (.in0(I1), .in1(LData), .out(RI1), .sel(LoadRAM));
  Multiplexer #(.width(32), .enable("false")) multiplexer_3 (.in0(I2), .in1(LData), .out(RI2), .sel(LoadRAM));
  Multiplexer #(.width(32), .enable("false")) multiplexer_4 (.in0(I3), .in1(LData), .out(RI3), .sel(LoadRAM));
  and and_1 (LoadRAM, ~1'b1, LoadRAMOn);  // AND_Gate
  Multiplexer #(.width(16), .enable("false")) multiplexer_5 (.in0(Addr), .in1(LAddr), .out(RAddr), .sel(LoadRAM));
  Multiplexer #(.width(4), .enable("false")) multiplexer_6 (.in0(Mask), .in1(LMask), .out(RMask), .sel(LoadRAM));
  Multiplexer #(.enable("false")) multiplexer_7 (.in0(CS), .in1(LW), .out(RCS), .sel(LoadRAM));
  Multiplexer #(.enable("false")) multiplexer_8 (.in0(R_W), .in1(LW), .out(R_R_W), .sel(LoadRAM));

  // Notes on the sheet:
  //   NO MODIFICAR
  //   Keyboard
endmodule

module S_MIPS (
  input  Kbd_Available,
  input  [6:0] Kbd_ASCII_Data,
  input  [31:0] RAM_Out_0,
  input  [31:0] RAM_Out_1,
  input  Reset,
  input  [31:0] RAM_Out_2,
  input  Clock,
  input  [31:0] RAM_Out_3,
  input  [3:0] Read_Time,
  input  [3:0] Write_Time,
  output Kbd_Enable,
  output [15:0] Address,
  output Kbd_Clear,
  output TTY_Enable,
  output [6:0] TTY_ASCII_Data,
  output Stop,
  output [31:0] RAM_In_0,
  output [31:0] RAM_In_1,
  output [31:0] RAM_In_2,
  output [31:0] RAM_In_3,
  output [3:0] Mask,
  output nRead_Write,
  output Chip_Select
);

  wire not_1_out;

  not not_1 (not_1_out, Reset);
  CPU___Final cpu_final_1 (
    .WT(Write_Time), .RT(Read_Time), .clk(Clock), .start(not_1_out), .rst(Reset), .D1(RAM_Out_0),
    .D2(RAM_Out_1), .D3(RAM_Out_2), .D4(RAM_Out_3), .TTY_ENABLE(TTY_Enable), .D_Out(RAM_In_0),
    .TTY_DATA(TTY_ASCII_Data), .END(Stop), .RAM_Adress(Address), .CS(Chip_Select), .RAM_R_W(nRead_Write),
    .MASK(Mask), .in_10(Kbd_Available), .in_11(Kbd_ASCII_Data), .kbd_En(Kbd_Enable));

  assign RAM_In_1 = RAM_In_0;
  assign RAM_In_2 = RAM_In_0;
  assign RAM_In_3 = RAM_In_0;

  // Other names for the same wires on the sheet: CLK = Clock; CLR = Reset; CS = Chip_Select;
  //   KBD_AVAIL = Kbd_Available; KBD_CLR = Kbd_Clear; KBD_DATA[6:0] = Kbd_ASCII_Data; RAM_A[15:0] = Address;
  //   RAM_INPUT_0[31:0] = RAM_In_0; RAM_INPUT_1[31:0] = RAM_In_0; RAM_INPUT_2[31:0] = RAM_In_0;
  //   RAM_INPUT_3[31:0] = RAM_In_0; RAM_MASK[3:0] = Mask; RAM_OUTPUT_0[31:0] = RAM_Out_0;
  //   RAM_OUTPUT_1[31:0] = RAM_Out_1; RAM_OUTPUT_2[31:0] = RAM_Out_2; RAM_OUTPUT_3[31:0] = RAM_Out_3;
  //   RW = nRead_Write; TTY_DATA[6:0] = TTY_ASCII_Data

  // Notes on the sheet:
  //   RAM ADDRESS
  //   DATA FROM RAM
  //   DATA TO RAM
  //   DATA WRITE MASK
  //   RAM TIMING
  //   RAM CONTROL
  //   KEYBOARD
  //   TTY
  //   SEQUENCING
endmodule

module RAM (
  input  [15:0] Address,
  input  [31:0] Data_In_0,
  input  [31:0] Data_In_1,
  input  [31:0] Data_In_2,
  input  [31:0] Data_In_3,
  input  [3:0] Mask,
  input  nRead_Write,
  input  Chip_Select,
  input  Reset,
  output [31:0] Data_Out_0,
  output [31:0] Data_Out_1,
  output [31:0] Data_Out_2,
  output [31:0] Data_Out_3,
  output [3:0] Read_Time,
  output [3:0] Write_Time
);

  wire and_2_out, and_3_out, and_4_out, and_5_out, and_6_out, and_7_out, and_8_out, and_9_out, Changed, CLK,
       comparator_2_eq, comparator_3_eq, comparator_4_eq, comparator_5_eq, comparator_6_eq, Count,
       demultiplexer_3_out0, Idle, Idle_q, Load, Load0, Load1, nand_1_out, or_1_out, or_2_out, or_3_out,
       or_4_out, or_5_out, or_6_out, or_7_out, or_8_out, or_9_out, or_10_out, Proc_q, Update_Mem, Zero_Time;
  wire [3:0] counter_1_q, multiplexer_1_out, subtractor_1_out;
  wire [31:0] register_1_q, register_2_q, register_3_q, register_4_q, register_5_q;

  // Probe on 4'b0011
  // Probe on 4'b0010
  Multiplexer #(.width(4), .enable("false")) multiplexer_1 (
    .in0(4'b0011), .in1(4'b0010), .out(multiplexer_1_out), .sel(nRead_Write));
  or or_1 (or_1_out, Idle, Update_Mem);
  or or_2 (or_2_out, ~Chip_Select, Reset);  // OR_Gate
  Subtractor #(.width(4)) subtractor_1 (.a(multiplexer_1_out), .b(4'b0010), .out(subtractor_1_out));  // open: bin, bout
  Demultiplexer #(.enable("false")) demultiplexer_1 (.out0(Idle), .out1(Load0), .in(Idle_q), .sel(Changed));
  D_Flip_Flop u_Idle (.clk(CLK), .D(or_1_out), .Q(Idle_q), .preset(or_2_out));  // open: Qn, en, reset
  // Probe on {{11{1'b1}}, nRead_Write, Mask, Address}
  // Probe on counter_1_q
  Counter #(.width(4), .max('hf)) counter_1 (
    .load(Load), .D(subtractor_1_out), .count(Count), .Q(counter_1_q), .clk(CLK), .clr(or_3_out));  // open: carry
  or or_3 (or_3_out, ~Chip_Select, Reset);  // OR_Gate
  Comparator #(.width(4), .mode("unsigned")) comparator_1 (
    .a(4'b0000), .b(counter_1_q), .eq(Zero_Time));  // open: gt, lt
  or or_4 (or_4_out, Count, Load0, Load1);
  Register #(.width(32)) register_1 (.D(Data_In_0), .en(Chip_Select), .Q(register_1_q), .clk(CLK), .clr(or_5_out));
  or or_5 (or_5_out, ~Chip_Select, Reset);  // OR_Gate
  Register #(.width(32)) register_2 (.D(Data_In_1), .en(Chip_Select), .Q(register_2_q), .clk(CLK), .clr(or_6_out));
  or or_6 (or_6_out, ~Chip_Select, Reset);  // OR_Gate
  Register #(.width(32)) register_3 (.D(Data_In_2), .en(Chip_Select), .Q(register_3_q), .clk(CLK), .clr(or_7_out));
  or or_7 (or_7_out, ~Chip_Select, Reset);  // OR_Gate
  Register #(.width(32)) register_4 (.D(Data_In_3), .en(Chip_Select), .Q(register_4_q), .clk(CLK), .clr(or_8_out));
  or or_8 (or_8_out, ~Chip_Select, Reset);  // OR_Gate
  Register #(.width(32)) register_5 (
    .D({{11{1'b1}}, nRead_Write, Mask, Address}), .en(Chip_Select), .Q(register_5_q), .clk(CLK),
    .clr(or_9_out));
  or or_9 (or_9_out, ~Chip_Select, Reset);  // OR_Gate
  D_Flip_Flop Proc (.clk(CLK), .D(or_4_out), .Q(Proc_q), .reset(or_10_out));  // open: Qn, preset, en
  or or_10 (or_10_out, ~Chip_Select, Reset);  // OR_Gate
  // Probe on register_5_q
  Demultiplexer #(.enable("false")) demultiplexer_2 (
    .out0(Count), .out1(Update_Mem), .in(demultiplexer_3_out0), .sel(Zero_Time));
  Demultiplexer #(.enable("false")) demultiplexer_3 (
    .out0(demultiplexer_3_out0), .out1(Load1), .in(Proc_q), .sel(Changed));
  Clock clock_1 (.out(CLK));
  Comparator #(.width(32)) comparator_2 (.a(register_1_q), .b(Data_In_0), .eq(comparator_2_eq));  // open: gt, lt
  Comparator #(.width(32)) comparator_3 (.a(register_2_q), .b(Data_In_1), .eq(comparator_3_eq));  // open: gt, lt
  Comparator #(.width(32)) comparator_4 (.a(register_3_q), .b(Data_In_2), .eq(comparator_4_eq));  // open: gt, lt
  Comparator #(.width(32)) comparator_5 (.a(register_4_q), .b(Data_In_3), .eq(comparator_5_eq));  // open: gt, lt
  Comparator #(.width(32)) comparator_6 (
    .a(register_5_q), .b({{11{1'b1}}, nRead_Write, Mask, Address}), .eq(comparator_6_eq));  // open: gt, lt
  nand nand_1 (nand_1_out, comparator_6_eq, comparator_2_eq, comparator_3_eq, comparator_4_eq, comparator_5_eq);
  and and_1 (Changed, nand_1_out, Chip_Select);
  or or_11 (Load, Count, Load1, Load0);
  and and_2 (and_2_out, Mask[0], Update_Mem, nRead_Write);
  and and_3 (and_3_out, Mask[1], Update_Mem, nRead_Write);
  and and_4 (and_4_out, Mask[2], Update_Mem, nRead_Write);
  and and_5 (and_5_out, Mask[3], Update_Mem, nRead_Write);
  RAM_part #(.addrWidth(16), .dataWidth(32), .bus("separate")) ram_1 (
    .addr(Address), .din(Data_In_0), .data(Data_Out_0), .str(and_2_out), .sel(Chip_Select), .clk(CLK),
    .ld(and_6_out), .clr(Reset));
  and and_6 (and_6_out, ~nRead_Write, Idle);  // AND_Gate
  RAM_part #(.addrWidth(16), .dataWidth(32), .bus("separate")) ram_2 (
    .addr(Address), .din(Data_In_1), .data(Data_Out_1), .str(and_3_out), .sel(Chip_Select), .clk(CLK),
    .ld(and_7_out), .clr(Reset));
  and and_7 (and_7_out, ~nRead_Write, Idle);  // AND_Gate
  RAM_part #(.addrWidth(16), .dataWidth(32), .bus("separate")) ram_3 (
    .addr(Address), .din(Data_In_2), .data(Data_Out_2), .str(and_4_out), .sel(Chip_Select), .clk(CLK),
    .ld(and_8_out), .clr(Reset));
  and and_8 (and_8_out, ~nRead_Write, Idle);  // AND_Gate
  RAM_part #(.addrWidth(16), .dataWidth(32), .bus("separate")) ram_4 (
    .addr(Address), .din(Data_In_3), .data(Data_Out_3), .str(and_5_out), .sel(Chip_Select), .clk(CLK),
    .ld(and_9_out), .clr(Reset));
  and and_9 (and_9_out, ~nRead_Write, Idle);  // AND_Gate

  assign Read_Time = 4'b0011;
  assign Write_Time = 4'b0010;

  // Other names for the same wires on the sheet: M0 = Mask[0]; M1 = Mask[1]; M2 = Mask[2]; M3 = Mask[3];
  //   RW = nRead_Write; CLR = Reset; CS = Chip_Select; Load2 = Count

  // Notes on the sheet:
  //   NO MODIFICAR
  //   excepto quizás los valores RT y WT
  //   BANK0
  //   BANK1
  //   BANK2
  //   BANK3
endmodule

module RAM_Dispatcher (
  input  [3:0] WriteTime,
  input  Clock,
  input  CLR,
  output [31:0] Data,
  output [15:0] Address,
  output [3:0] Mask,
  output Finished,
  output Write
);

  wire demultiplexer_2_out1, demultiplexer_3_out1, End, IDLE_q, IncAddr, Load, or_1_out, or_2_out, While_q,
       WriteEnd;
  wire [3:0] counter_1_q;
  wire [31:0] CurrentAddress_q;

  Counter #(.width(32), .max('hffffffff)) CurrentAddress (
    .count(IncAddr), .Q({CurrentAddress_q[31:18], Address, CurrentAddress_q[1:0]}), .clk(Clock), .clr(CLR));  // open: load, D, carry
  or or_1 (or_1_out, IncAddr, demultiplexer_3_out1, Finished);
  D_Flip_Flop IDLE (.clk(Clock), .D(or_1_out), .Q(IDLE_q), .preset(CLR));  // open: Qn, en, reset
  Demultiplexer #(.enable("false")) demultiplexer_1 (.out0(Load), .out1(Finished), .in(IDLE_q), .sel(End));
  D_Flip_Flop While (.clk(Clock), .D(or_2_out), .Q(While_q), .reset(CLR));  // open: Qn, preset, en
  or or_2 (or_2_out, Write, Load);
  RAM_part #(.addrWidth(18), .dataWidth(32)) ram_1 (
    .addr({Address, CurrentAddress_q[1:0]}), .data(Data), .clk(Clock));  // open: sel, ld, clr
  Demultiplexer #(.enable("false")) demultiplexer_2 (
    .out0(Write), .out1(demultiplexer_2_out1), .in(While_q), .sel(WriteEnd));
  Decoder #(.select(2)) decoder_1 (
    .out0(Mask[0]), .out1(Mask[1]), .out2(Mask[2]), .out3(Mask[3]), .sel(CurrentAddress_q[1:0]));  // open: en
  Demultiplexer #(.enable("false")) demultiplexer_3 (
    .out0(IncAddr), .out1(demultiplexer_3_out1), .in(demultiplexer_2_out1), .sel(End));
  Counter #(.width(4), .max('hf)) counter_1 (
    .load(Load), .D(WriteTime), .count(Write), .Q(counter_1_q), .clk(Clock));  // open: carry, clr
  Comparator #(.width(32)) comparator_1 (.a(Data), .b({32{1'b1}}), .eq(End));  // open: gt, lt
  Comparator #(.width(4)) comparator_2 (.a(4'b0000), .b(counter_1_q), .eq(WriteEnd));  // open: gt, lt

  // Other names for the same wires on the sheet: CLK = Clock; Count = Write; WT[3:0] = WriteTime
endmodule

module CPU___Final (
  input  [3:0] WT,
  input  [3:0] RT,
  input  clk,
  input  start,
  input  rst,
  input  [31:0] D1,
  input  [31:0] D2,
  input  [31:0] D3,
  input  [31:0] D4,
  input  in_10,
  input  [6:0] in_11,
  output kbd_En,
  output TTY_ENABLE,
  output [31:0] D_Out,
  output [6:0] TTY_DATA,
  output END,
  output [15:0] RAM_Adress,
  output CS,
  output RAM_R_W,
  output [3:0] MASK
);

  wire ALU_Load, c_IR, D_Load, f_ALU, Hi_Lo_Sel, HiLo_Load, I, I_O_D, IR_Load, J, jr, L_En, PC_En, pop_2,
       push, R, RF_R_W;
  wire [1:0] ALU_A, ALU_B, RF_D_SEL;
  wire [3:0] ALU_Op;
  wire [5:0] func_code, op_code;

  Control_Unit control_unit_1 (
    .DATA_Load(D_Load), .in_1(clk), .in_2(RT), .in_3(WT), .in_4(rst), .in_5(start), .in_6(R), .in_7(op_code),
    .in_8(I), .in_9(func_code), .in_10(J), .END(END), .PC_Load(PC_En), .Sel_A(ALU_A), .Loads_Enable(L_En),
    .Sel_B(ALU_B), .ALU_OP(ALU_Op), .CS(CS), .out_25(Hi_Lo_Sel), .out_26(HiLo_Load), .out_28(jr),
    .out_31(push), .tty(TTY_ENABLE), .IR_Load(IR_Load), .out_29(RF_D_SEL), .out_30(RF_R_W), .pop2(pop_2),
    .RAM_R_W(RAM_R_W), .kbd_En(kbd_En), .Use_ALU(ALU_Load), .load_from_ALU(f_ALU), .clr_instr(c_IR),
    .I_O_D(I_O_D));
  DataPath___main datapath_main_1 (
    .in_1(push), .in_2(ALU_Op), .in_3(D1), .in_4(pop_2), .in_5(ALU_A), .in_6(jr), .in_7(ALU_B), .in_8(D2),
    .in_9(RF_R_W), .in_10(HiLo_Load), .in_11(RF_D_SEL), .in_12(Hi_Lo_Sel), .in_15(I_O_D), .in_13(D3),
    .in_16(L_En), .in_17(IR_Load), .in_18(clk), .in_19(D_Load), .in_21(rst), .in_22(PC_En), .in_20(D4),
    .out_28(op_code), .out_29(func_code), .TTY_DATA(TTY_DATA), .out_32(I), .out_33(J), .out_34(R),
    .D_RAM_OUT(D_Out), .in_14(RAM_R_W), .RAM_DIR(RAM_Adress), .MASK(MASK), .in_23(in_11), .in_24(in_10),
    .in_25(ALU_Load), .in_27(f_ALU), .in_26(c_IR));

  // Other names for the same wires on the sheet: D_To_RAM[31:0] = D_Out; KBD_AV = in_10; KBD_DATA[6:0] = in_11;
  //   RAM_Adr[15:0] = RAM_Adress; TTY_En = TTY_ENABLE

  // Notes on the sheet:
  //   RAM TIME
  //   CPU - ASM
  //   RAM DATA IN
  //   KEYBOARD IN
  //   RAM OUT
  //   SCREEN
endmodule

module Control_Unit (
  input  in_1,
  input  [3:0] in_2,
  input  [3:0] in_3,
  input  in_4,
  input  in_5,
  input  in_6,
  input  [5:0] in_7,
  input  in_8,
  input  [5:0] in_9,
  input  in_10,
  output PC_Load,
  output END,
  output IR_Load,
  output load_from_ALU,
  output clr_instr,
  output pop2,
  output DATA_Load,
  output I_O_D,
  output Use_ALU,
  output [1:0] Sel_A,
  output Loads_Enable,
  output [1:0] Sel_B,
  output [3:0] ALU_OP,
  output CS,
  output out_25,
  output out_26,
  output tty,
  output out_28,
  output [1:0] out_29,
  output out_30,
  output out_31,
  output kbd_En,
  output RAM_R_W
);

  wire d_ff_1_q, d_ff_3_q, demultiplexer_1_out0, demultiplexer_1_out1, demultiplexer_2_out0,
       demultiplexer_3_out0, demultiplexer_3_out1, demultiplexer_4_out0, demultiplexer_4_out1,
       demultiplexer_5_out0, demultiplexer_6_out0, demultiplexer_6_out1, demultiplexer_7_out1,
       demultiplexer_8_out0, demultiplexer_9_out0, end_R0, end_R1, end_W, EXECUTE_q, is_halt, Loads_En0,
       Loads_En3, Loads_En4, lw, NEXT_q, or_1_out, or_2_out, or_3_out, or_4_out, or_8_out, or_9_out,
       or_10_out, R_RAM, rst_wait, SP___4, sw, tty_t, Use_ALU_2, Use_ALU_t, USE_RAM_0, USE_RAM_1, USE_RAM_2;
  wire [3:0] ALU_SEL;

  D_Flip_Flop d_ff_1 (.clk(in_1), .D(demultiplexer_1_out0), .Q(d_ff_1_q), .preset(in_4));  // open: Qn, en, reset
  Demultiplexer #(.disabled(0), .enable("false")) demultiplexer_1 (
    .out0(demultiplexer_1_out0), .out1(demultiplexer_1_out1), .in(d_ff_1_q), .sel(in_5));
  or or_1 (or_1_out, PC_Load, demultiplexer_1_out1);
  D_Flip_Flop FETCH (.clk(in_1), .D(or_1_out), .Q(clr_instr), .reset(in_4));  // open: Qn, preset, en
  or or_2 (or_2_out, demultiplexer_2_out0, clr_instr);
  Get_Signals get_signals_1 (
    .R(in_6), .I(in_8), .J(in_10), .Op_Code(in_7), .Func_Code(in_9), .Push(out_31), .HiLo_Sel(out_25),
    .RF_Sel(out_29), .Load_HiLo(out_26), .RF_R_W(out_30), .Halt(is_halt), .tty(tty_t), .Pop(I_O_D),
    .Jr(out_28), .R_Ram(R_RAM), .W_Ram(RAM_R_W), .lw(lw), .sw(sw), .KBD_En(kbd_En));
  Demultiplexer #(.disabled(0), .enable("false")) demultiplexer_2 (
    .out0(demultiplexer_2_out0), .out1(IR_Load), .in(USE_RAM_0), .sel(end_R0));
  D_Flip_Flop \wait  (.clk(in_1), .D(or_2_out), .Q(USE_RAM_0), .reset(in_4));  // open: Qn, preset, en
  Waiter waiter_1 (.in_1(in_2), .in_2(in_1), .in_3(rst_wait), .in_4(clr_instr), .\end (end_R0));
  Demultiplexer #(.disabled(0), .enable("false")) demultiplexer_3 (
    .out0(demultiplexer_3_out0), .out1(demultiplexer_3_out1), .in(EXECUTE_q), .sel(is_halt));
  D_Flip_Flop EXECUTE (.clk(in_1), .D(IR_Load), .Q(EXECUTE_q), .reset(in_4));  // open: Qn, preset, en
  or or_3 (or_3_out, END, demultiplexer_3_out1);
  Demultiplexer #(.disabled(0), .enable("false")) demultiplexer_4 (
    .out0(demultiplexer_4_out0), .out1(demultiplexer_4_out1), .in(demultiplexer_3_out0), .sel(R_RAM));
  ALU_Decoder alu_decoder_1 (
    .in_1(in_7), .in_2(in_9), .in_3(in_6), .in_4(in_8), .in_7(in_10), .ALU_SEL(ALU_SEL), .Sel_A(Sel_A),
    .Sel_B(Sel_B), .Pop(I_O_D), .Push(out_31), .lw(lw), .sw(sw), .Use_ALU(Use_ALU_t));
  D_Flip_Flop u_END (.clk(in_1), .D(or_3_out), .Q(END), .reset(in_4));  // open: Qn, preset, en
  or or_4 (or_4_out, demultiplexer_5_out0, demultiplexer_4_out1);
  Waiter waiter_2 (.in_1(in_2), .in_2(in_1), .in_3(rst_wait), .in_4(demultiplexer_4_out1), .\end (end_R1));
  Demultiplexer #(.disabled(0), .enable("false")) demultiplexer_5 (
    .out0(demultiplexer_5_out0), .out1(DATA_Load), .in(USE_RAM_1), .sel(end_R1));
  D_Flip_Flop WAIT_2 (.clk(in_1), .D(or_4_out), .Q(USE_RAM_1), .reset(in_4));  // open: Qn, preset, en
  Demultiplexer #(.disabled(0), .enable("false")) demultiplexer_6 (
    .out0(demultiplexer_6_out0), .out1(demultiplexer_6_out1), .in(DATA_Load), .sel(I_O_D));
  or or_5 (Loads_Enable, Loads_En0, DATA_Load, pop2, Loads_En3, Loads_En4);
  or or_6 (CS, USE_RAM_0, USE_RAM_1, USE_RAM_2);
  D_Flip_Flop WAIT_3 (.clk(in_1), .D(demultiplexer_6_out1), .Q(Loads_En4), .reset(in_4));  // open: Qn, preset, en
  D_Flip_Flop WAIT_4 (.clk(in_1), .D(Loads_En4), .Q(SP___4), .reset(in_4));  // open: Qn, preset, en
  or or_7 (rst_wait, PC_Load, in_4);
  and and_1 (tty, tty_t, Loads_Enable);
  D_Flip_Flop WAIT_5 (.clk(in_1), .D(SP___4), .Q(pop2), .reset(in_4));  // open: Qn, preset, en
  Multiplexer #(.width(4), .disabled(0), .enable("false")) multiplexer_1 (
    .in0(ALU_SEL), .in1(4'b0000), .out(ALU_OP), .sel(SP___4));
  Demultiplexer #(.disabled(0), .enable("false")) demultiplexer_7 (
    .out0(Loads_En0), .out1(demultiplexer_7_out1), .in(or_8_out), .sel(RAM_R_W));
  or or_8 (or_8_out, demultiplexer_4_out0, demultiplexer_6_out0, pop2);
  or or_9 (or_9_out, demultiplexer_8_out0, demultiplexer_7_out1);
  D_Flip_Flop WAIT_6 (.clk(in_1), .D(or_9_out), .Q(USE_RAM_2), .reset(in_4));  // open: Qn, preset, en
  Waiter waiter_3 (.in_1(in_3), .in_2(in_1), .in_3(rst_wait), .in_4(demultiplexer_7_out1), .\end (end_W));
  Demultiplexer #(.disabled(0), .enable("false")) demultiplexer_8 (
    .out0(demultiplexer_8_out0), .out1(Use_ALU_2), .in(USE_RAM_2), .sel(end_W));
  or or_10 (or_10_out, Loads_En0, Loads_En3);
  D_Flip_Flop d_ff_2 (.clk(in_1), .D(Use_ALU_2), .Q(Loads_En3));  // open: Qn, preset, en, reset
  D_Flip_Flop NEXT (.clk(in_1), .D(or_10_out), .Q(NEXT_q), .reset(in_4));  // open: Qn, preset, en
  Demultiplexer #(.disabled(0), .enable("false")) demultiplexer_9 (
    .out0(demultiplexer_9_out0), .out1(load_from_ALU), .in(NEXT_q), .sel(Use_ALU_t));
  or or_11 (Use_ALU, Use_ALU_t, Use_ALU_2, SP___4);
  or or_12 (PC_Load, demultiplexer_9_out0, d_ff_3_q);
  D_Flip_Flop d_ff_3 (.clk(in_1), .D(load_from_ALU), .Q(d_ff_3_q), .reset(in_4));  // open: Qn, preset, en

  // Other names for the same wires on the sheet: clk = in_1; func_code[5:0] = in_9; I = in_8; J = in_10; jr = out_28;
  //   L_En = Loads_Enable; Loads_En1 = DATA_Load; Loads_En2 = pop2; op_code[5:0] = in_7; pop = I_O_D; push = out_31;
  //   R = in_6; rst = in_4; rst_w = PC_Load; RT[3:0] = in_2; start = in_5; Use_ALU_3 = SP___4; W_RAM = RAM_R_W;
  //   WT[3:0] = in_3
endmodule

module Waiter (
  input  [3:0] in_1,
  input  in_2,
  input  in_3,
  input  in_4,
  output \end 
);

  wire and_1_out, load, not_1_out;
  wire [3:0] i;

  not not_1 (not_1_out, \end );
  Counter #(.width(4), .max('hf), .ongoal("stay")) counter (
    .count(and_1_out), .Q(i), .clk(in_2), .clr(in_3));  // open: load, D, carry
  and and_1 (and_1_out, load, not_1_out);
  D_Flip_Flop d_ff_1 (.clk(in_2), .Q(load), .preset(in_4), .reset(in_3));  // open: D, Qn, en
  Comparator #(.width(4), .mode("unsigned")) comparator_1 (.a(i), .b(in_1), .gt(\end ));  // open: eq, lt

  // Other names for the same wires on the sheet: clk = in_2; rst = in_3; start = in_4; t[3:0] = in_1

  // Notes on the sheet:
  //   WAITER
endmodule

module ALU_Decoder (
  input  [5:0] in_1,
  input  [5:0] in_2,
  input  in_3,
  input  in_4,
  input  Pop,
  input  lw,
  input  in_7,
  input  Push,
  input  sw,
  output [1:0] Sel_A,
  output Use_ALU,
  output [3:0] ALU_SEL,
  output [1:0] Sel_B
);

  wire addi, and_2_out, andi, beq, bgtz, blez, bltz, bne, branch, comparator_2_eq, comparator_9_lt,
       comparator_10_gt, comparator_11_eq, decoder_1_out11, do_A, I_Arith, mfhi, mflo, no_alu_0000, OP_0000,
       Op_00, or_1_out, or_3_out, or_5_out, or_6_out, or_7_out, ori, R_ALU, slt, slti, sltiu, sltu,
       special_R, \xor , xorii;
  wire [1:0] Sel_B_I, Sel_B_R;
  wire [3:0] ALU_SEL_I, ALU_SEL_R, priority_encoder_1_out;

  // Probe on 6'b101000
  // Probe on 6'b101010
  // Probe on 6'b101011
  // Probe on 6'b010000
  // Probe on 6'b010010
  Multiplexer #(.width(2), .disabled(0), .enable("false")) multiplexer_1 (
    .in0(2'b00), .in1(2'b01), .out(Sel_B_R), .sel(or_1_out));
  or or_1 (or_1_out, Pop, Push);
  or or_2 (do_A, mfhi, mflo, Pop);
  Multiplexer #(.width(2), .disabled(0), .enable("false")) multiplexer_2 (
    .in0(Sel_B_R), .in1(2'b10), .out(Sel_A), .sel(or_3_out));
  or or_3 (or_3_out, mfhi, mflo);
  Comparator #(.width(3), .mode("unsigned")) comparator_1 (.a(in_1[5:3]), .b(3'b000), .eq(branch));  // open: gt, lt
  Comparator #(.width(3), .mode("unsigned")) comparator_2 (
    .a(in_1[5:3]), .b(3'b001), .eq(comparator_2_eq));  // open: gt, lt
  Comparator #(.width(6), .mode("unsigned")) comparator_3 (.a(in_2), .b(6'b101000), .eq(\xor ));  // open: gt, lt
  Comparator #(.width(6), .mode("unsigned")) comparator_4 (.a(in_2), .b(6'b101010), .eq(slt));  // open: gt, lt
  Comparator #(.width(6), .mode("unsigned")) comparator_5 (.a(in_2), .b(6'b101011), .eq(sltu));  // open: gt, lt
  Comparator #(.width(6), .mode("unsigned")) comparator_6 (.a(in_2), .b(6'b010000), .eq(mfhi));  // open: gt, lt
  Comparator #(.width(6), .mode("unsigned")) comparator_7 (.a(in_2), .b(6'b010010), .eq(mflo));  // open: gt, lt
  and and_1 (I_Arith, comparator_2_eq, in_4);
  // Probe on in_1[3:0]
  Multiplexer #(.width(4), .disabled(0), .enable("false")) multiplexer_3 (
    .in0(ALU_SEL_R), .in1(ALU_SEL_I), .out(ALU_SEL), .sel(in_4));
  Multiplexer #(.width(2), .disabled(0), .enable("false")) multiplexer_4 (
    .in0(2'b10), .in1(2'b00), .out(Sel_B_I), .sel(branch));
  Priority_Encoder #(.select(4), .disabled(0)) priority_encoder_1 (
    .in2(Push), .in6(\xor ), .in12(slt), .in13(sltu), .in15(do_A), .out(priority_encoder_1_out));  // open: in0, in1, in3, in4, in5, in7, in8, in9, in10, in11, in14, gs, en_out, en_in
  or or_4 (special_R, \xor , slt, sltu, do_A, Push);
  Comparator #(.width(6), .mode("unsigned")) comparator_8 (.a(in_1), .b({6{1'b0}}), .eq(OP_0000));  // open: gt, lt
  Comparator #(.width(6), .mode("unsigned")) comparator_9 (
    .a(in_2), .b(6'b011100), .lt(comparator_9_lt));  // open: gt, eq
  Comparator #(.width(6), .mode("unsigned")) comparator_10 (
    .a(in_2), .b(6'b010111), .gt(comparator_10_gt));  // open: eq, lt
  Comparator #(.width(6), .mode("unsigned")) comparator_11 (
    .a(in_2), .b(6'b001000), .eq(comparator_11_eq));  // open: gt, lt
  Multiplexer #(.width(4), .disabled(0), .enable("false")) multiplexer_5 (
    .in0(in_2[3:0]), .in1(priority_encoder_1_out), .out(ALU_SEL_R), .sel(special_R));
  Multiplexer #(.width(2), .disabled(0), .enable("false")) multiplexer_6 (
    .in0(Sel_B_R), .in1(Sel_B_I), .out(Sel_B), .sel(in_4));
  and and_2 (and_2_out, comparator_9_lt, comparator_10_gt);
  and and_3 (R_ALU, OP_0000, no_alu_0000);
  nor nor_1 (no_alu_0000, and_2_out, comparator_11_eq);
  Decoder #(.select(4), .enable("false")) decoder_1 (
    .out1(bltz), .out4(beq), .out5(bne), .out6(blez), .out7(bgtz), .out8(addi), .out10(slti),
    .out11(decoder_1_out11), .out12(andi), .out13(ori), .out14(xorii), .sel(in_1[3:0]));  // open: out0, out2, out3, out9, out15
  or or_5 (or_5_out, addi, lw, sw);
  or or_6 (or_6_out, beq, bne);
  or or_7 (or_7_out, blez, bltz, bgtz);
  or or_8 (Use_ALU, R_ALU, I_Arith);
  Priority_Encoder #(.select(4), .disabled(0)) priority_encoder_2 (
    .in0(or_5_out), .in2(or_6_out), .in4(andi), .in5(ori), .in6(xorii), .in12(slti), .in13(sltiu),
    .in15(or_7_out), .out(ALU_SEL_I));  // open: in1, in3, in7, in8, in9, in10, in11, in14, gs, en_out, en_in
  and and_4 (sltiu, decoder_1_out11, Op_00);

  // Other names for the same wires on the sheet: Four[3:0] = in_2[3:0]; func_code[5:0] = in_2; Two[1:0] = in_2[5:4];
  //   I = in_4; J = in_7; op_code[5:0] = in_1; OP_Four[3:0] = in_1[3:0]; OP_Two[1:0] = in_1[5:4]; R = in_3

  // Notes on the sheet:
  //   ALU Op
  //   ALU Sel
  //   Use ALU
  //   ALU DECODER
  //   Specials R
  //   (sus ultimos 4 dig del op code no coincide con el ALU op)
  //   SELECTORES A Y B
  //   TYPE R
  //   TYPE I
endmodule

module Get_Signals (
  input  [5:0] Op_Code,
  input  [5:0] Func_Code,
  input  R,
  input  I,
  input  J,
  output Halt,
  output tty,
  output KBD_En,
  output Pop,
  output Push,
  output lw,
  output Jr,
  output R_Ram,
  output W_Ram,
  output sw,
  output Load_HiLo,
  output HiLo_Sel,
  output [1:0] RF_Sel,
  output RF_R_W
);

  wire Arithmetic_I, comparator_7_eq, comparator_8_eq, comparator_9_eq, comparator_10_eq, comparator_11_gt,
       comparator_12_lt, comparator_13_eq, comparator_14_eq, comparator_15_eq, F_00_0001, mfhi, nF_00_0001,
       nor_1_out, nor_2_out, Op_11_1111, OP___0, OP____0, Op_push_pop, or_1_out, RF_R_W_Type_I,
       RF_R_W_Type_R, rnd;

  Comparator #(.width(6), .mode("unsigned")) comparator_1 (
    .a(Op_Code), .b({6{1'b1}}), .eq(Op_11_1111));  // open: gt, lt
  Comparator #(.width(6), .mode("unsigned")) comparator_2 (.a(Op_Code), .b({6{1'b0}}), .eq(OP___0));  // open: gt, lt
  Comparator #(.width(6), .mode("unsigned")) comparator_3 (
    .a(Func_Code), .b(6'b000001), .eq(F_00_0001));  // open: gt, lt
  Comparator #(.width(6), .mode("unsigned")) comparator_4 (
    .a(Op_Code), .b(6'b111000), .eq(Op_push_pop));  // open: gt, lt
  Comparator #(.width(6), .mode("unsigned")) comparator_5 (.a(Op_Code), .b(6'b100011), .eq(lw));  // open: gt, lt
  Comparator #(.width(6), .mode("unsigned")) comparator_6 (.a(Op_Code), .b(6'b101011), .eq(sw));  // open: gt, lt
  not not_1 (OP____0, OP___0);
  not not_2 (nF_00_0001, F_00_0001);
  Comparator #(.width(6), .mode("unsigned")) comparator_7 (
    .a(Func_Code), .b(6'b010010), .eq(comparator_7_eq));  // open: gt, lt
  Comparator #(.width(6), .mode("unsigned")) comparator_8 (
    .a(Func_Code), .b(6'b010000), .eq(comparator_8_eq));  // open: gt, lt
  or or_1 (or_1_out, lw, Pop);
  nor nor_1 (nor_1_out, Halt, tty, Jr, Load_HiLo);
  and and_1 (HiLo_Sel, OP___0, comparator_7_eq);
  and and_2 (mfhi, OP___0, comparator_8_eq);
  and and_3 (RF_R_W_Type_R, R, nor_1_out);
  nor nor_2 (nor_2_out, rnd, or_1_out, KBD_En);
  // Probe on 6'b011100
  Priority_Encoder #(.select(2), .disabled(0)) priority_encoder_1 (
    .in0(nor_2_out), .in1(KBD_En), .in2(or_1_out), .in3(rnd), .out(RF_Sel));  // open: gs, en_out, en_in
  Comparator #(.width(6), .mode("unsigned")) comparator_9 (
    .a(Func_Code), .b({6{1'b1}}), .eq(comparator_9_eq));  // open: gt, lt
  and and_4 (tty, Op_11_1111, F_00_0001);
  and and_5 (Pop, Op_push_pop, nF_00_0001);
  and and_6 (Jr, OP___0, comparator_10_eq);
  Comparator #(.width(6), .mode("unsigned")) comparator_10 (
    .a(Func_Code), .b(6'b001000), .eq(comparator_10_eq));  // open: gt, lt
  Comparator #(.width(6), .mode("unsigned")) comparator_11 (
    .a(Func_Code), .b(6'b010111), .gt(comparator_11_gt));  // open: eq, lt
  Comparator #(.width(6), .mode("unsigned")) comparator_12 (
    .a(Func_Code), .b(6'b011100), .lt(comparator_12_lt));  // open: gt, eq
  or or_2 (RF_R_W_Type_I, lw, Arithmetic_I);
  and and_7 (Halt, Op_11_1111, comparator_9_eq);
  and and_8 (Load_HiLo, OP___0, comparator_11_gt, comparator_12_lt);
  or or_3 (RF_R_W, RF_R_W_Type_R, RF_R_W_Type_I);
  Comparator #(.width(6), .mode("unsigned")) comparator_13 (
    .a(Func_Code), .b(6'b000010), .eq(comparator_13_eq));  // open: gt, lt
  Comparator #(.width(6), .mode("unsigned")) comparator_14 (
    .a(Func_Code), .b(6'b000011), .eq(comparator_14_eq));  // open: gt, lt
  and and_9 (Push, Op_push_pop, F_00_0001);
  or or_4 (R_Ram, lw, Pop);
  and and_10 (rnd, Op_11_1111, comparator_13_eq);
  and and_11 (KBD_En, Op_11_1111, comparator_14_eq);
  or or_5 (W_Ram, sw, Push);
  Comparator #(.width(3), .mode("unsigned")) comparator_15 (
    .a(Op_Code[5:3]), .b(3'b001), .eq(comparator_15_eq));  // open: gt, lt
  and and_12 (Arithmetic_I, I, comparator_15_eq);

  // Other names for the same wires on the sheet: Hilo_L = Load_HiLo; kbd = KBD_En; mflo = HiLo_Sel

  // Notes on the sheet:
  //   Instruction Interpreter
endmodule

module DataPath___main (
  input  in_1,
  input  [3:0] in_2,
  input  [31:0] in_3,
  input  in_4,
  input  [1:0] in_5,
  input  in_6,
  input  [1:0] in_7,
  input  [31:0] in_8,
  input  in_9,
  input  in_10,
  input  [1:0] in_11,
  input  in_12,
  input  [31:0] in_13,
  input  in_14,
  input  in_15,
  input  in_16,
  input  in_17,
  input  in_18,
  input  in_19,
  input  [31:0] in_20,
  input  in_21,
  input  in_22,
  input  [6:0] in_23,
  input  in_24,
  input  in_25,
  input  in_26,
  input  in_27,
  output [5:0] out_28,
  output [5:0] out_29,
  output [6:0] TTY_DATA,
  output [31:0] D_RAM_OUT,
  output out_32,
  output out_33,
  output out_34,
  output [15:0] RAM_DIR,
  output [3:0] MASK
);

  wire and_1_out, and_2_out, and_3_out, FC, jmp, N, or_1_out, or_2_out, or_3_out, Z;
  wire [1:0] multiplexer_8_out;
  wire [4:0] A3, multiplexer_5_out, Rd, Rs, Rt;
  wire [6:0] multiplexer_2_out;
  wire [15:0] k, Ram_adress, Ram_W_Adress;
  wire [27:0] D;
  wire [31:0] ALU_F, ALU_Hi, ALU_OUT, B, branch_control_1_ia_prime, \const , DIR, Hi, Hi_Lo, IA,
       instr_fetcher_1_data_from_ram, instruction, KBD_Out, Lo, multiplexer_1_out, multiplexer_3_out,
       multiplexer_4_out, multiplexer_9_out, multiplexer_12_out, multiplexer_13_out, Ram_Out, SP, ticks;
  wire [31:7] A;

  // Probe on branch_control_1_ia_prime
  Multiplexer #(.width(32), .disabled(0), .enable("false")) multiplexer_1 (
    .in0(DIR), .in1({A, TTY_DATA}), .out(multiplexer_1_out), .sel(in_6));
  Multiplexer #(.width(7), .disabled(0), .enable("false")) multiplexer_2 (
    .in0({7{1'b1}}), .in1(in_23), .out(multiplexer_2_out), .sel(in_24));
  assign KBD_Out = {{25{1'b0}}, multiplexer_2_out};  // Bit_Extender bit_extender_1
  Flag_Condition_Switch flag_condition_switch_1 (.in_1(out_28), .in_2(Z), .in_3(N), .in_4(out_32), .FC(FC));
  Branch_Control branch_control_1 (
    .in_2(IA), .in_3(jmp), .in_4(FC), .IA_prime(branch_control_1_ia_prime), .in_1(multiplexer_1_out));
  // Probe on IA
  Program_Counter program_counter_1 (
    .in_1(branch_control_1_ia_prime), .in_2(in_22), .in_3(in_21), .in_4(in_18), .out_5(IA));
  Multiplexer #(.width(32), .disabled(0), .enable("false")) multiplexer_3 (
    .in0(B), .in1({A, TTY_DATA}), .out(multiplexer_3_out), .sel(in_1));
  Multiplexer #(.width(32), .disabled(0), .enable("false")) multiplexer_4 (
    .in0(IA), .in1(ALU_F), .out(multiplexer_4_out), .sel(in_15));
  Constant_Completer constant_completer_1 (.in_1(out_28), .in_2(k), .\const (\const ));
  Instr_Fetcher instr_fetcher_1 (
    .in_1(in_3), .in_2(in_8), .in_3(in_13), .in_4(in_20), .in_5(multiplexer_4_out), .out_7(Ram_adress),
    .Data_From_RAM(instr_fetcher_1_data_from_ram));
  // Probe on instr_fetcher_1_data_from_ram
  RAM_Storer ram_storer_1 (.in_1(multiplexer_3_out), .in_2(ALU_F), .value(D_RAM_OUT), .adr(Ram_W_Adress), .out_5(MASK));
  // Probe on \const 
  // Probe on instr_fetcher_1_data_from_ram
  Multiplexer #(.width(5), .disabled(0), .enable("false")) multiplexer_5 (
    .in0(Rd), .in1(Rt), .out(multiplexer_5_out), .sel(out_32));
  or or_1 (or_1_out, in_1, in_4);
  Multiplexer #(.width(5), .disabled(0), .enable("false")) multiplexer_6 (
    .in0(multiplexer_5_out), .in1({5{1'b1}}), .out(A3), .sel(or_1_out));
  Register #(.width(32)) IR (
    .D(instr_fetcher_1_data_from_ram), .en(in_17), .Q(instruction), .clk(in_18), .clr(or_2_out));
  or or_2 (or_2_out, in_21, in_26);
  Register #(.width(32)) Data (.D(instr_fetcher_1_data_from_ram), .en(in_19), .Q(Ram_Out), .clk(in_18), .clr(in_21));
  Multiplexer #(.width(32), .disabled(0), .enable("false")) multiplexer_7 (
    .in0(\const ), .in1({IA[31:28], D}), .out(DIR), .sel(out_33));
  // Probe on ALU_OUT
  Multiplexer #(.width(2), .disabled(0), .enable("false")) multiplexer_8 (
    .in0(in_11), .in1(2'b00), .out(multiplexer_8_out), .sel(in_4));
  or or_3 (or_3_out, in_16, in_27);
  Multiplexer #(.select(2), .width(32), .disabled(0), .enable("false")) multiplexer_9 (
    .in0(ALU_OUT), .in1(KBD_Out), .in2(Ram_Out), .in3(ticks), .out(multiplexer_9_out), .sel(multiplexer_8_out));
  // Probe on multiplexer_8_out
  and and_1 (and_1_out, in_9, or_3_out);
  or or_4 (jmp, in_6, out_33);
  Instruction_Decoder instruction_decoder_1 (
    .in_1(instruction), .I(out_32), .out_3(out_28), .J(out_33), .R(out_34), .func_code(out_29), .Rd(Rd),
    .Rt(Rt), .Rs(Rs), .Dest(D), .out_11(k));
  Register_File register_file_1 (
    .in_1(multiplexer_9_out), .DA(A3), .in_3(and_1_out), .SA(Rs), .in_5(in_21), .SB(Rt), .in_7(in_18),
    .A({A, TTY_DATA}), .B(B), .SP(SP));
  Multiplexer #(.width(16), .disabled(0), .enable("false")) multiplexer_10 (
    .in0(Ram_adress), .in1(Ram_W_Adress), .out(RAM_DIR), .sel(in_14));
  Multiplexer #(.width(32), .disabled(0), .enable("false")) multiplexer_11 (
    .in0(Hi), .in1(Lo), .out(Hi_Lo), .sel(in_12));
  Multiplexer #(.select(2), .width(32), .disabled(0), .enable("false")) multiplexer_12 (
    .in0(B), .in1(32'h4), .in2(\const ), .out(multiplexer_12_out), .sel(in_7));  // open: in3
  and and_2 (and_2_out, in_10, in_16);
  // Probe on multiplexer_13_out
  Multiplexer #(.select(2), .width(32), .disabled(0), .enable("false")) multiplexer_13 (
    .in0({A, TTY_DATA}), .in1(SP), .in2(Hi_Lo), .out(multiplexer_13_out), .sel(in_5));  // open: in3
  // Probe on multiplexer_12_out
  Register #(.width(32)) register_1 (.D(ALU_Hi), .en(and_2_out), .Q(Hi), .clk(in_18), .clr(in_21));
  Counter #(.width(32), .max('hffffffff)) Tick_Count (
    .count(1'b1), .Q(ticks), .clk(in_18));  // open: load, D, carry, clr
  // Probe on ALU_F
  ALU_2 alu_1 (
    .Output(ALU_F), .Z_Flag(Z), .Hi(ALU_Hi), .A(multiplexer_13_out), .B(multiplexer_12_out), .SEL(in_2),
    .N_Flagt(N));
  and and_3 (and_3_out, in_10, in_16);
  Register #(.width(32)) register_2 (.D(ALU_F), .en(and_3_out), .Q(Lo), .clk(in_18), .clr(in_21));
  // Probe on ALU_OUT
  Register #(.width(32)) register_3 (.D(ALU_F), .en(in_25), .Q(ALU_OUT), .clk(in_18), .clr(in_21));

  // Other names for the same wires on the sheet: A[6:0] = TTY_DATA; ALU_Op[3:0] = in_2; ALU_SEL_A[1:0] = in_5;
  //   ALU_SEL_B[1:0] = in_7; clk = in_18; clr_IR = in_26; Data_Load = in_19; DATA_RAM_2[31:0] = in_8;
  //   DATA_RAM_3[31:0] = in_13; DATA_RAM_4[31:0] = in_20; DATA_RAM__1[31:0] = in_3; DATA_RAM_OUT[31:0] = D_RAM_OUT;
  //   from_ALU = in_27; Hi_Lo_Sel = in_12; HiLo_Load = in_10; I = out_32; I_or_D = in_15; IR_Load = in_17; J = out_33;
  //   J_Dir[31:0] = {IA[31:28], D}; jr = in_6; KBD_AVAIBLE = in_24; KBD_D[6:0] = in_23; L_En = in_16;
  //   op_code[5:0] = out_28; PC_en = in_22; pop2 = in_4; push = in_1; R = out_34; RAM_RW = in_14;
  //   RF_D_SEL[1:0] = in_11; RF_R_W = in_9; rst = in_21; Use_ALU = in_25

  // Notes on the sheet:
  //   RAM
endmodule

module Branch_Control (
  input  [31:0] in_1,
  input  [31:0] in_2,
  input  in_3,
  input  in_4,
  output [31:0] IA_prime
);

  wire [31:0] adder_1_out, IA_prime_prime, multiplexer_1_out;

  Adder #(.width(32)) adder_1 (.a(in_2), .b(32'h4), .out(adder_1_out));  // open: cin, cout
  Multiplexer #(.width(32), .disabled(0), .enable("false")) multiplexer_1 (
    .in0({32{1'b0}}), .in1(in_1), .out(multiplexer_1_out), .sel(in_4));
  Adder #(.width(32)) adder_2 (.a(adder_1_out), .b(multiplexer_1_out), .out(IA_prime_prime));  // open: cin, cout
  Multiplexer #(.width(32), .disabled(0), .enable("false")) multiplexer_2 (
    .in0(IA_prime_prime), .in1(in_1), .out(IA_prime), .sel(in_3));

  // Other names for the same wires on the sheet: FC = in_4; IA[31:0] = in_2; J_Size[31:0] = in_1; jmp = in_3

  // Notes on the sheet:
  //   BRANCH CONTROL
endmodule

module Flag_Condition_Switch (
  input  [5:0] in_1,
  input  in_2,
  input  in_3,
  input  in_4,
  output FC
);

  wire _000, A, and_1_out, and_6_out, B, beq, bgtz, blez, bltz, bne, C, D, E, nor_1_out, or_1_out, or_2_out;

  Decoder #(.select(3), .disabled(0), .enable("false")) decoder_1 (
    .out1(bltz), .out4(beq), .out5(bne), .out6(blez), .out7(bgtz), .sel(in_1[2:0]));  // open: out0, out2, out3
  Comparator #(.width(3)) comparator_1 (.a(in_1[5:3]), .b(3'b000), .eq(_000));  // open: gt, lt
  and and_1 (and_1_out, in_4, _000);
  and and_2 (A, bne, ~in_2);  // AND_Gate
  and and_3 (B, beq, in_2);
  and and_4 (C, blez, or_1_out);
  or or_1 (or_1_out, in_2, in_3);
  or or_2 (or_2_out, A, B, C, D, E);
  and and_5 (FC, or_2_out, and_1_out);
  nor nor_1 (nor_1_out, in_2, in_3);
  and and_6 (and_6_out, in_3, ~in_2);  // AND_Gate
  and and_7 (D, bgtz, nor_1_out);
  and and_8 (E, bltz, and_6_out);

  // Other names for the same wires on the sheet: I = in_4; N_Flag = in_3; Last_3[2:0] = in_1[2:0];
  //   op_code[5:0] = in_1; First_3[2:0] = in_1[5:3]; Z_Flag = in_2

  // Notes on the sheet:
  //   Flags Condition
endmodule

module Program_Counter (
  input  [31:0] in_1,
  input  in_2,
  input  in_3,
  input  in_4,
  output [31:0] out_5
);

  Register #(.width(32)) PC (.D(in_1), .en(in_2), .Q(out_5), .clk(in_4), .clr(in_3));

  // Other names for the same wires on the sheet: clk = in_4; en = in_2; PC[31:0] = out_5; PC_prime[31:0] = in_1;
  //   rst = in_3

  // Notes on the sheet:
  //   Program Counter
endmodule

module Instr_Fetcher (
  input  [31:0] in_1,
  input  [31:0] in_2,
  input  [31:0] in_3,
  input  [31:0] in_4,
  input  [31:0] in_5,
  output [31:0] Data_From_RAM,
  output [15:0] out_7
);

  Multiplexer #(.select(2), .width(32), .disabled(0), .enable("false")) multiplexer_1 (
    .in0(in_1), .in1(in_2), .in2(in_3), .in3(in_4),
    .out({Data_From_RAM[7:0], Data_From_RAM[15:8], Data_From_RAM[23:16], Data_From_RAM[31:24]}),
    .sel(in_5[3:2]));
  // Probe on in_5[3:2]

  assign out_7 = in_5[19:4];

  // Other names for the same wires on the sheet: adress[31:0] = in_5; DATA_SEL[1:0] = in_5[3:2];
  //   RAM_ADRESS[15:0] = in_5[19:4]; DATA_RAM_2[31:0] = in_2; DATA_RAM_3[31:0] = in_3; DATA_RAM_4[31:0] = in_4;
  //   DATA_RAM__1[31:0] = in_1

  // Notes on the sheet:
  //   RAM Fetcher
  //   aqui
endmodule

module RAM_Storer (
  input  [31:0] in_1,
  input  [31:0] in_2,
  output [31:0] value,
  output [15:0] adr,
  output [3:0] out_5
);

  // Probe on in_1
  Multiplexer #(.select(2), .width(4), .disabled(0), .enable("false")) multiplexer_1 (
    .in0(4'b0001), .in1(4'b0010), .in2(4'b0100), .in3(4'b1000), .out(out_5), .sel(in_2[3:2]));

  assign adr = in_2[19:4];
  assign value = {in_1[7:0], in_1[15:8], in_1[23:16], in_1[31:24]};

  // Other names for the same wires on the sheet: dir[31:0] = in_2; MASK[1:0] = in_2[3:2]

  // Notes on the sheet:
  //   RAM STORER
  //   aqui
endmodule

module Instruction_Decoder (
  input  [31:0] in_1,
  output I,
  output [5:0] out_3,
  output J,
  output R,
  output [5:0] func_code,
  output [4:0] Rd,
  output [4:0] Rt,
  output [4:0] Rs,
  output [27:0] Dest,
  output [15:0] out_11
);

  Type_Decoder type_decoder_1 (.in_1(in_1[31:26]), .I(I), .J(J), .R(R));

  assign Dest = {in_1[25:0], 2'b00};
  assign func_code = in_1[5:0];
  assign out_3 = in_1[31:26];
  assign out_11 = in_1[15:0];
  assign Rd = in_1[15:11];
  assign Rs = in_1[25:21];
  assign Rt = in_1[20:16];

  // Other names for the same wires on the sheet: D[25:0] = in_1[25:0]; instruct[31:0] = in_1; k[15:0] = in_1[15:0];
  //   op_code[5:0] = in_1[31:26]

  // Notes on the sheet:
  //   INSTRUCTION DECODER
endmodule

module Type_Decoder (
  input  [5:0] in_1,
  output I,
  output J,
  output R
);

  wire and_1_out, and_3_out, and_4_out, D___E___F___V___nD___nE___nF, nA___nB___nC, nD___nE___nF;

  nor nor_1 (nD___nE___nF, in_1[2], in_1[1], in_1[0]);
  and and_1 (and_1_out, in_1[2], in_1[1], in_1[0]);
  and and_2 (J, nA___nB___nC, ~in_1[2], in_1[1], ~in_1[0]);  // AND_Gate
  or or_1 (D___E___F___V___nD___nE___nF, nD___nE___nF, and_1_out);
  nor nor_2 (nA___nB___nC, in_1[5], in_1[4], in_1[3]);
  and and_3 (and_3_out, nA___nB___nC, nD___nE___nF);
  and and_4 (and_4_out, in_1[5], in_1[4], in_1[3], D___E___F___V___nD___nE___nF);
  or or_2 (R, and_3_out, and_4_out);
  nor nor_3 (I, J, R);

  // Other names for the same wires on the sheet: F = in_1[0]; E = in_1[1]; D = in_1[2]; C = in_1[3]; B = in_1[4];
  //   A = in_1[5]

  // Notes on the sheet:
  //   TYPE DECODER
endmodule

module Register_File (
  input  [31:0] in_1,
  input  [4:0] DA,
  input  in_3,
  input  [4:0] SA,
  input  in_5,
  input  [4:0] SB,
  input  in_7,
  output [31:0] A,
  output [31:0] SP,
  output [31:0] B
);

  wire a0, a1, a2, a3, a4, a5, a6, a7, a8, a9, a10, a11, a12, a13, a14, a15, a16, a17, a18, a19, a20, a21,
       a22, a23, a24, a25, a26, a27, a28, a29, a30, a31;
  wire [31:0] q0, q1, q2, q3, q4, q5, q6, q7, q8, q9, q10, q11, q12, q13, q14, q15, q16, q17, q18, q19, q20,
       q21, q22, q23, q24, q25, q26, q27, q28, q29, q30;

  Decoder #(.select(5), .disabled(0)) decoder_1 (
    .out0(a0), .out1(a1), .out2(a2), .out3(a3), .out4(a4), .out5(a5), .out6(a6), .out7(a7), .out8(a8),
    .out9(a9), .out10(a10), .out11(a11), .out12(a12), .out13(a13), .out14(a14), .out15(a15), .out16(a16),
    .out17(a17), .out18(a18), .out19(a19), .out20(a20), .out21(a21), .out22(a22), .out23(a23), .out24(a24),
    .out25(a25), .out26(a26), .out27(a27), .out28(a28), .out29(a29), .out30(a30), .out31(a31), .sel(DA),
    .en(in_3));
  Register #(.width(32)) R0 (.D({32{1'b0}}), .en(a0), .Q(q0), .clk(in_7), .clr(in_5));
  Register #(.width(32)) R4 (.D(in_1), .en(a4), .Q(q4), .clk(in_7), .clr(in_5));
  Register #(.width(32)) R8 (.D(in_1), .en(a8), .Q(q8), .clk(in_7), .clr(in_5));
  Register #(.width(32)) R12 (.D(in_1), .en(a12), .Q(q12), .clk(in_7), .clr(in_5));
  Register #(.width(32)) R16 (.D(in_1), .en(a16), .Q(q16), .clk(in_7), .clr(in_5));
  Register #(.width(32)) R20 (.D(in_1), .en(a20), .Q(q20), .clk(in_7), .clr(in_5));
  Register #(.width(32)) R24 (.D(in_1), .en(a24), .Q(q24), .clk(in_7), .clr(in_5));
  Register #(.width(32)) R28 (.D(in_1), .en(a28), .Q(q28), .clk(in_7), .clr(in_5));
  Register #(.width(32)) R1 (.D(in_1), .en(a1), .Q(q1), .clk(in_7), .clr(in_5));
  Register #(.width(32)) R5 (.D(in_1), .en(a5), .Q(q5), .clk(in_7), .clr(in_5));
  Register #(.width(32)) R9 (.D(in_1), .en(a9), .Q(q9), .clk(in_7), .clr(in_5));
  Register #(.width(32)) R13 (.D(in_1), .en(a13), .Q(q13), .clk(in_7), .clr(in_5));
  Register #(.width(32)) R17 (.D(in_1), .en(a17), .Q(q17), .clk(in_7), .clr(in_5));
  Register #(.width(32)) R21 (.D(in_1), .en(a21), .Q(q21), .clk(in_7), .clr(in_5));
  Register #(.width(32)) R25 (.D(in_1), .en(a25), .Q(q25), .clk(in_7), .clr(in_5));
  Register #(.width(32)) R29 (.D(in_1), .en(a29), .Q(q29), .clk(in_7), .clr(in_5));
  // Probe on q29
  Register #(.width(32)) R2 (.D(in_1), .en(a2), .Q(q2), .clk(in_7), .clr(in_5));
  Register #(.width(32)) R6 (.D(in_1), .en(a6), .Q(q6), .clk(in_7), .clr(in_5));
  Register #(.width(32)) R10 (.D(in_1), .en(a10), .Q(q10), .clk(in_7), .clr(in_5));
  Register #(.width(32)) R14 (.D(in_1), .en(a14), .Q(q14), .clk(in_7), .clr(in_5));
  Register #(.width(32)) R18 (.D(in_1), .en(a18), .Q(q18), .clk(in_7), .clr(in_5));
  Register #(.width(32)) R22 (.D(in_1), .en(a22), .Q(q22), .clk(in_7), .clr(in_5));
  Register #(.width(32)) R26 (.D(in_1), .en(a26), .Q(q26), .clk(in_7), .clr(in_5));
  Register #(.width(32)) R30 (.D(in_1), .en(a30), .Q(q30), .clk(in_7), .clr(in_5));
  Register #(.width(32)) R3 (.D(in_1), .en(a3), .Q(q3), .clk(in_7), .clr(in_5));
  Register #(.width(32)) R7 (.D(in_1), .en(a7), .Q(q7), .clk(in_7), .clr(in_5));
  Register #(.width(32)) R11 (.D(in_1), .en(a11), .Q(q11), .clk(in_7), .clr(in_5));
  Register #(.width(32)) R15 (.D(in_1), .en(a15), .Q(q15), .clk(in_7), .clr(in_5));
  Register #(.width(32)) R19 (.D(in_1), .en(a19), .Q(q19), .clk(in_7), .clr(in_5));
  Register #(.width(32)) R23 (.D(in_1), .en(a23), .Q(q23), .clk(in_7), .clr(in_5));
  Register #(.width(32)) R27 (.D(in_1), .en(a27), .Q(q27), .clk(in_7), .clr(in_5));
  Register #(.width(32)) R31 (.D(in_1), .en(a31), .Q(SP), .clk(in_7), .clr(in_5));
  Multiplexer #(.select(5), .width(32), .enable("false")) multiplexer_1 (
    .in0(q0), .in1(q1), .in2(q2), .in3(q3), .in4(q4), .in5(q5), .in6(q6), .in7(q7), .in8(q8), .in9(q9),
    .in10(q10), .in11(q11), .in12(q12), .in13(q13), .in14(q14), .in15(q15), .in16(q16), .in17(q17),
    .in18(q18), .in19(q19), .in20(q20), .in21(q21), .in22(q22), .in23(q23), .in24(q24), .in25(q25),
    .in26(q26), .in27(q27), .in28(q28), .in29(q29), .in30(q30), .in31(SP), .out(A), .sel(SA));
  Multiplexer #(.select(5), .width(32), .enable("false")) multiplexer_2 (
    .in0(q0), .in1(q1), .in2(q2), .in3(q3), .in4(q4), .in5(q5), .in6(q6), .in7(q7), .in8(q8), .in9(q9),
    .in10(q10), .in11(q11), .in12(q12), .in13(q13), .in14(q14), .in15(q15), .in16(q16), .in17(q17),
    .in18(q18), .in19(q19), .in20(q20), .in21(q21), .in22(q22), .in23(q23), .in24(q24), .in25(q25),
    .in26(q26), .in27(q27), .in28(q28), .in29(q29), .in30(q30), .in31(SP), .out(B), .sel(SB));

  // Other names for the same wires on the sheet: clk = in_7; DI[31:0] = in_1; q31[31:0] = SP; R_W = in_3; rst = in_5

  // Notes on the sheet:
  //   REGISTER FILE
  //   Control Signals
  //   Input Register
  //   Registers
  //   Output Registers
endmodule

module ALU_2 (
  input  [31:0] A,
  input  [31:0] B,
  input  [3:0] SEL,
  output [31:0] Output,
  output Z_Flag,
  output N_Flagt,
  output [31:0] Hi
);

  wire comparator_1_lt, comparator_2_lt;
  wire [31:0] adder_1_out, and_1_out, bit_extender_1_out, bit_extender_2_out, divider_1_out,
       divisor_con_signo_1_div, Hi_Sign, Hi_t, multip_con_signo_1_lo, multiplier_1_out, nor_1_out, or_1_out,
       Rest, Rest_Sign, subtractor_1_out, xor_1_out;

  Adder #(.width(32)) adder_1 (.a(A), .b(B), .out(adder_1_out));  // open: cin, cout
  Subtractor #(.width(32)) subtractor_1 (.a(A), .b(B), .out(subtractor_1_out));  // open: bin, bout
  assign and_1_out = A & B;  // AND_Gate and_1, 32 bits wide
  assign or_1_out = A | B;  // OR_Gate or_1, 32 bits wide
  assign xor_1_out = A ^ B;  // XOR_Gate xor_1, 32 bits wide
  assign nor_1_out = ~(A | B);  // NOR_Gate nor_1, 32 bits wide
  Multiplier #(.width(32)) multiplier_1 (.a(A), .b(B), .out(multiplier_1_out), .cout(Hi_t));  // open: cin
  Multip_con_Signo multip_con_signo_1 (.A(A), .B(B), .Lo(multip_con_signo_1_lo), .Hi(Hi_Sign));
  Divider #(.width(32)) divider_1 (.a(A), .b(B), .out(divider_1_out), .rem(Rest));  // open: upper
  Divisor_con_Signo divisor_con_signo_1 (.A(A), .B(B), .Div(divisor_con_signo_1_div), .Rest(Rest_Sign));
  Comparator #(.width(32)) comparator_1 (.a(A), .b(B), .lt(comparator_1_lt));  // open: gt, eq
  Comparator #(.width(32), .mode("unsigned")) comparator_2 (.a(A), .b(B), .lt(comparator_2_lt));  // open: gt, eq
  assign bit_extender_1_out = {{31{1'b0}}, comparator_1_lt};  // Bit_Extender bit_extender_1
  assign bit_extender_2_out = {{31{1'b0}}, comparator_2_lt};  // Bit_Extender bit_extender_2
  Multiplexer #(.select(4), .width(32), .disabled(0), .enable("false")) multiplexer_1 (
    .in0(adder_1_out), .in1({32{1'b0}}), .in2(subtractor_1_out), .in3({32{1'b0}}), .in4(and_1_out),
    .in5(or_1_out), .in6(xor_1_out), .in7(nor_1_out), .in8(multiplier_1_out), .in9(multip_con_signo_1_lo),
    .in10(divider_1_out), .in11(divisor_con_signo_1_div), .in12(bit_extender_1_out),
    .in13(bit_extender_2_out), .in14({32{1'b0}}), .in15(A), .out(Output), .sel(SEL));
  Multiplexer #(.select(2), .width(32), .enable("false")) multiplexer_2 (
    .in0(Hi_t), .in1(Hi_Sign), .in2(Rest), .in3(Rest_Sign), .out(Hi), .sel(SEL[1:0]));
  // Probe on SEL[1:0]
  Comparator #(.width(32)) comparator_3 (.a(Output), .b({32{1'b0}}), .eq(Z_Flag), .lt(N_Flagt));  // open: gt

  // Other names for the same wires on the sheet: Selector[3:0] = SEL

  // Notes on the sheet:
  //   ARITHMETIC LOGIC UNIT(ALU)
endmodule

module Divisor_con_Signo (
  input  [31:0] A,
  input  [31:0] B,
  output [31:0] Div,
  output [31:0] Rest
);

  wire [30:0] Com_a2_A, Com_a2_B, Current, multiplexer_1_out, multiplexer_2_out, negator_3_out;

  Negator #(.width(31)) negator_1 (.in(A[30:0]), .out(Com_a2_A));
  Negator #(.width(31)) negator_2 (.in(B[30:0]), .out(Com_a2_B));
  xor xor_1 (Div[31], B[31], A[31]);
  Multiplexer #(.width(31), .enable("false")) multiplexer_1 (
    .in0(A[30:0]), .in1(Com_a2_A), .out(multiplexer_1_out), .sel(A[31]));
  Multiplexer #(.width(31), .enable("false")) multiplexer_2 (
    .in0(B[30:0]), .in1(Com_a2_B), .out(multiplexer_2_out), .sel(B[31]));
  Negator #(.width(31)) negator_3 (.in(Current), .out(negator_3_out));
  Multiplexer #(.width(31), .enable("false")) multiplexer_3 (
    .in0(Current), .in1(negator_3_out), .out(Div[30:0]), .sel(Div[31]));
  Divider #(.width(31)) divider_1 (
    .a(multiplexer_1_out), .b(multiplexer_2_out), .out(Current), .rem(Rest[30:0]));  // open: upper

  assign Rest[31] = 1'b0;

  // Other names for the same wires on the sheet: A_t[30:0] = A[30:0]; Sign_A = A[31]; B_t[30:0] = B[30:0];
  //   Sign_B = B[31]; Div_t[30:0] = Div[30:0]; Sign = Div[31]; Rest_t[30:0] = Rest[30:0]

  // Notes on the sheet:
  //   Divisor Con Signo
endmodule

module Multip_con_Signo (
  input  [31:0] A,
  input  [31:0] B,
  output [31:0] Lo,
  output [31:0] Hi
);

  wire [30:0] Com_a2_A, Com_a2_B, multiplexer_1_out, multiplexer_2_out;

  Negator #(.width(31)) negator_1 (.in(A[30:0]), .out(Com_a2_A));
  Negator #(.width(31)) negator_2 (.in(B[30:0]), .out(Com_a2_B));
  xor xor_1 (Hi[31], B[31], A[31]);
  Multiplexer #(.width(31), .enable("false")) multiplexer_1 (
    .in0(A[30:0]), .in1(Com_a2_A), .out(multiplexer_1_out), .sel(A[31]));
  Multiplexer #(.width(31), .enable("false")) multiplexer_2 (
    .in0(B[30:0]), .in1(Com_a2_B), .out(multiplexer_2_out), .sel(B[31]));
  Multiplier #(.width(31)) multiplier_1 (
    .a(multiplexer_1_out), .b(multiplexer_2_out), .out(Lo[30:0]), .cout({Hi[29:0], Lo[31]}));  // open: cin

  assign Hi[30] = 1'b0;

  // Other names for the same wires on the sheet: A_t[30:0] = A[30:0]; Sign_A = A[31]; B_t[30:0] = B[30:0];
  //   Sign_B = B[31]; Hi_Mult[30:0] = {Hi[29:0], Lo[31]}; Sign = Hi[31]; Mult[30:0] = Lo[30:0]
endmodule

module Constant_Completer (
  input  [5:0] in_1,
  input  [15:0] in_2,
  output [31:0] \const 
);

  wire branch_comp, zero_comp;
  wire [31:0] multiplexer_1_out, sign_k, zero_k;
  wire [31:18] branch_k;

  assign branch_k = {{13{in_2[15]}}, in_2[15]};  // Bit_Extender bit_extender_1
  assign zero_k = {{16{1'b0}}, in_2};  // Bit_Extender bit_extender_2
  assign sign_k = {{16{in_2[15]}}, in_2};  // Bit_Extender bit_extender_3
  Comparator #(.width(3), .mode("unsigned")) comparator_1 (
    .a(in_1[5:3]), .b(3'b000), .eq(branch_comp));  // open: gt, lt
  Comparator #(.width(4), .mode("unsigned")) comparator_2 (.a(in_1[5:2]), .b(4'b0011), .eq(zero_comp));  // open: gt, lt
  Multiplexer #(.width(32), .disabled(0), .enable("false")) multiplexer_1 (
    .in0(sign_k), .in1({branch_k, in_2, 2'b00}), .out(multiplexer_1_out), .sel(branch_comp));
  Multiplexer #(.width(32), .disabled(0), .enable("false")) multiplexer_2 (
    .in0(multiplexer_1_out), .in1(zero_k), .out(\const ), .sel(zero_comp));

  // Other names for the same wires on the sheet: branch_k[17:2] = in_2; k[15:0] = in_2; k_15 = in_2[15];
  //   op_code[5:0] = in_1; First_4[3:0] = in_1[5:2]; First_3[2:0] = in_1[5:3]

  // Notes on the sheet:
  //   Constant Completer
endmodule
